// Logisim project ZY1501_U201514902_汤汇川_cpu_动态分支预测.circ as structural Verilog: 10 circuits, main circuit cpu
module cpu (
);

  wire A_EX, A_MEM, alu_1_p5, and_1_out, and_2_out, and_3_out, and_4_out, and_5_out, and_6_out, and_7_out,
       and_8_out, and_9_out, and_10_out, and_11_out, and_12_out, and_13_out, and_14_out, and_15_out,
       and_16_out, and_18_out, and_19_out, and_20_out, B_EX, B_MEM, beq, Bequal, bgez, bht_1_hit, bne,
       branch_Suc, clk, cmp, comparator_1_eq, comparator_2_eq, comparator_3_gt, control_1_alusrc,
       control_1_beq, control_1_bgez, control_1_bne, control_1_jal, control_1_jr, control_1_jump,
       control_1_lh, control_1_memread, control_1_memwrite, control_1_regdst, control_1_regreadrb,
       control_1_regwrite, control_1_shift, control_1_syscall, control_1_zero_extend, equal, ex_mem_1_jalout,
       ex_mem_1_lh_2, ex_mem_1_memread_2, ex_mem_1_memwrite_2, ex_mem_1_regwrite_2, ex_mem_1_stopout,
       falsefetch, falsej, fly, Go, id_ex_1_a_exout, id_ex_1_a_memout, id_ex_1_alusrcout, id_ex_1_b_exout,
       id_ex_1_b_memout, id_ex_1_lhout, id_ex_1_memreadout, id_ex_1_memwriteout, id_ex_1_regwrite_2,
       if_id_1_predout, IR1, IR2, IR3, Jal, jal_t, Jr, Jump, lh, mem_wb_1_stopout, nop, nor_1_out, not_1_out,
       not_2_out, not_3_out, not_4_out, not_5_out, or_1_out, or_4_out, or_6_out, or_8_out, or_9_out,
       or_10_out, or_13_out, or_14_out, or_15_out, or_16_out, Pause, predj, RegWrite, RST, show, stop,
       syscall, W1, W2, W3, w_b, w_j, \暂停信号 ;
  wire [1:0] bht_1_nextstate;
  wire [3:0] control_1_aluop, id_ex_1_aluopout;
  wire [4:0] decoder_1_ra, decoder_1_rb, decoder_1_rw, ex_mem_1_rwout, id_ex_1_rwout, rW;
  wire [5:0] decoder_1_funct, decoder_1_opcode, decoder_1_scode, id_ex_1_tcodeout;
  wire [11:0] EX_PC, ID_PC, IF_PC;
  wire [15:0] adder_2_out, counter_5_q, \load_use次数 , \总周期数 , \插入气泡数 , \无条件分支指令数 , \有条件分支成功跳转 , \有条件分支指令数 ,
       \预测失败次数 , \预测成功次数 ;
  wire [27:0] decoder_1_pc, id_ex_1_pcout;
  wire [31:0] adder_1_out, alu_1_p6, alu_1_p7, baddr, bht_1_targetaddr, decoder_1_extend, ex_mem_1_npcout,
       ex_mem_1_rbout, id_ex_1_extendout, id_ex_1_raout, id_ex_1_rbout, if_id_1_irout, if_id_1_npcout,
       inAddr, mem_wb_1_drout, mips_ram_1_p7, multiplexer_1_out, multiplexer_2_out, multiplexer_3_out,
       multiplexer_4_out, multiplexer_5_out, multiplexer_7_out, multiplexer_8_out, multiplexer_9_out,
       multiplexer_10_out, multiplexer_11_out, multiplexer_12_out, multiplexer_13_out, multiplexer_14_out,
       NPC, PC_q, register_1_q, register_2_q, registerfile_1_p7, registerfile_1_p8, rom_1_data,
       shifter_1_out, SyscallOut, writeData;
  wire [31:16] multiplexer_15_out;

  Button \u_总复位  (.out(RST));
  Button _1 (.out(IR1));
  Button _2 (.out(IR2));
  Button _3 (.out(IR3));
  Multiplexer #(.width(32), .enable("false")) multiplexer_1 (
    .in0(multiplexer_2_out), .in1(bht_1_targetaddr), .out(multiplexer_1_out), .sel(and_2_out));
  not not_1 (not_1_out, or_1_out);
  or or_1 (or_1_out, Pause, Go, stop);
  Button \u_继续运行  (.out(Go));
  LED led_1 (.in(W1));
  LED led_2 (.in(W2));
  LED led_3 (.in(W3));
  // Probe on IF_PC
  and and_1 (and_1_out, predj, fly);
  and and_2 (and_2_out, bht_1_hit, bht_1_nextstate[1], ~falsej);  // AND_Gate
  Register #(.width(32)) PC (.D(multiplexer_1_out), .en(not_1_out), .Q(PC_q), .clk(clk), .clr(RST));
  Clock clock_1 (.out(clk));
  Hex_Digit_Display hex_digit_display_1 (.value(SyscallOut[31:28]));  // open: dp
  // Probe on ID_PC
  and and_3 (and_3_out, ~falsej, ~fly);  // AND_Gate
  Adder #(.width(32)) adder_1 (.a(32'h4), .b(PC_q), .out(adder_1_out));  // open: cin, cout
  BHT bht_1 (
    .nextAddr(multiplexer_3_out), .inAddr(inAddr), .w_b(w_b), .w_j(w_j), .clk(clk), .searchAddr(adder_1_out),
    .targetAddr(bht_1_targetaddr), .nextState(bht_1_nextstate), .success(fly), .hit(bht_1_hit));
  Counter #(.width(16), .max('hffff)) counter_1 (
    .count(fly), .Q(\插入气泡数 ), .clk(clk), .clr(RST));  // open: load, D, carry
  or or_2 (w_j, Jump, Jr, Jal);
  or or_3 (w_b, beq, bne, bgez);
  and and_4 (and_4_out, bne, ~Bequal);  // AND_Gate
  and and_5 (and_5_out, Bequal, beq);
  and and_6 (and_6_out, bgez, cmp);
  Hex_Digit_Display hex_digit_display_2 (.value(SyscallOut[27:24]));  // open: dp
  Hex_Digit_Display hex_digit_display_3 (.value(SyscallOut[23:20]));  // open: dp
  // Probe on multiplexer_4_out
  Multiplexer #(.width(32), .enable("false")) multiplexer_2 (
    .in0(multiplexer_4_out), .in1(adder_1_out), .out(multiplexer_2_out), .sel(or_4_out));
  or or_4 (or_4_out, and_3_out, and_1_out);
  // Probe on if_id_1_irout
  or or_5 (fly, Jump, Jr, Jal, branch_Suc);
  nor nor_1 (nor_1_out, stop, \暂停信号 );
  or or_6 (or_6_out, \暂停信号 , stop);
  or or_7 (branch_Suc, and_4_out, and_5_out, and_6_out);
  and and_7 (and_7_out, ~falsefetch, predj);  // AND_Gate
  Hex_Digit_Display hex_digit_display_4 (.value(SyscallOut[15:12]));  // open: dp
  Hex_Digit_Display hex_digit_display_5 (.value(SyscallOut[19:16]));  // open: dp
  // Probe on EX_PC
  Multiplexer #(.width(32), .enable("false")) multiplexer_3 (
    .in0(multiplexer_4_out), .in1(baddr), .out(multiplexer_3_out), .sel(w_b));
  IF_ID if_id_1 (
    .NPC(adder_1_out), .IR(rom_1_data), .NPCout(if_id_1_npcout), .IRout(if_id_1_irout), .clk(clk), .RST(RST),
    .branch(falsefetch), .pause(Pause), .pred(and_2_out), .predout(if_id_1_predout));
  ROM #(.addrWidth(10), .dataWidth(32)) rom_1 (.addr(PC_q[11:2]), .data(rom_1_data));  // open: sel
  Counter #(.width(16), .max('hffff)) counter_2 (
    .count(and_8_out), .Q(\无条件分支指令数 ), .clk(clk), .clr(RST));  // open: load, D, carry
  and and_8 (and_8_out, w_j, ~or_6_out);  // AND_Gate
  and and_9 (and_9_out, w_b, ~or_6_out);  // AND_Gate
  and and_10 (and_10_out, ~or_6_out, branch_Suc);  // AND_Gate
  Counter #(.width(16), .max('hffff)) counter_3 (
    .count(and_11_out), .Q(\预测失败次数 ), .clk(clk), .clr(RST));  // open: load, D, carry
  and and_11 (and_11_out, ~or_6_out, falsefetch);  // AND_Gate
  Counter #(.width(16), .max('hffff)) counter_4 (
    .count(and_12_out), .Q(\预测成功次数 ), .clk(clk), .clr(RST));  // open: load, D, carry
  and and_12 (and_12_out, ~or_6_out, and_7_out);  // AND_Gate
  Hex_Digit_Display hex_digit_display_6 (.value(SyscallOut[11:8]));  // open: dp
  Hex_Digit_Display hex_digit_display_7 (.value(SyscallOut[7:4]));  // open: dp
  // Probe on EX_PC
  Multiplexer #(.width(32), .enable("false")) multiplexer_4 (
    .in0(multiplexer_5_out), .in1(id_ex_1_raout), .out(multiplexer_4_out), .sel(Jr));
  Decoder decoder_1 (
    .CODE(if_id_1_irout), .PC(decoder_1_pc), .OPCODE(decoder_1_opcode), .FUNCT(decoder_1_funct),
    .RA(decoder_1_ra), .RB(decoder_1_rb), .RW(decoder_1_rw), .shift(control_1_shift),
    .RegDst(control_1_regdst), .syscall(control_1_syscall), .Jal(control_1_jal),
    .Zero_extend(control_1_zero_extend), .extend(decoder_1_extend), .sCODE(decoder_1_scode));
  Register #(.width(32)) register_1 (.D(if_id_1_irout), .Q(register_1_q), .clk(clk), .clr(RST));  // open: en
  Counter #(.width(16), .max('hffff)) counter_5 (
    .count(nor_1_out), .Q(counter_5_q), .clk(clk), .clr(RST));  // open: load, D, carry
  Counter #(.width(16), .max('hffff)) counter_6 (
    .count(and_13_out), .Q(\有条件分支指令数 ), .clk(clk), .clr(RST));  // open: load, D, carry
  and and_13 (and_13_out, and_9_out, ~nop);  // AND_Gate
  Counter #(.width(16), .max('hffff)) counter_7 (
    .count(and_14_out), .Q(\有条件分支成功跳转 ), .clk(clk), .clr(RST));  // open: load, D, carry
  and and_14 (and_14_out, and_10_out, ~nop);  // AND_Gate
  Hex_Digit_Display hex_digit_display_8 (.value(SyscallOut[3:0]));  // open: dp
  not not_2 (not_2_out, clk);
  Control control_1 (
    .ALUOP(control_1_aluop), .shift(control_1_shift), .Zero_extend(control_1_zero_extend),
    .ALUSrc(control_1_alusrc), .RegDst(control_1_regdst), .RegWrite(control_1_regwrite),
    .Jump(control_1_jump), .beq(control_1_beq), .bne(control_1_bne), .MemRead(control_1_memread),
    .MemWrite(control_1_memwrite), .Jal(control_1_jal), .jr(control_1_jr), .syscall(control_1_syscall),
    .bgez(control_1_bgez), .OPCODE(decoder_1_opcode), .FUNCT(decoder_1_funct), .lh(control_1_lh),
    .RegReadRB(control_1_regreadrb));
  Register #(.width(32)) register_2 (.D(register_1_q), .Q(register_2_q), .clk(clk), .clr(RST));  // open: en
  // Probe on register_2_q
  Adder #(.width(16)) adder_2 (.a(counter_5_q), .b(16'h2), .out(adder_2_out));  // open: cin, cout
  Multiplexer #(.width(32), .enable("false")) multiplexer_5 (
    .in0(multiplexer_7_out), .in1({inAddr[31:28], id_ex_1_pcout}), .out(multiplexer_5_out), .sel(Jump));
  not not_3 (not_3_out, control_1_jump);
  not not_4 (not_4_out, control_1_regreadrb);
  Multiplexer #(.width(16), .enable("false")) multiplexer_6 (
    .in0(counter_5_q), .in1(adder_2_out), .out(\总周期数 ), .sel(\暂停信号 ));
  Counter #(.width(16), .max('hffff)) counter_8 (
    .count(nop), .Q(\load_use次数 ), .clk(clk), .clr(RST));  // open: load, D, carry
  // Probe on \总周期数 
  // Probe on \无条件分支指令数 
  // Probe on \有条件分支成功跳转 
  // Probe on \load_use次数 
  // Probe on \预测失败次数 
  // Probe on \预测成功次数 
  Multiplexer #(.width(32), .enable("false")) multiplexer_7 (
    .in0(inAddr), .in1(baddr), .out(multiplexer_7_out), .sel(branch_Suc));
  // Probe on {inAddr[31:28], id_ex_1_pcout}
  // RegisterFile registerfile_1: pin names not known; wires that end beside it: writeData, not_2_out, RegWrite, rW, decoder_1_ra, decoder_1_rb, registerfile_1_p7, registerfile_1_p8
  nop nop_1 (
    .rW2(ex_mem_1_rwout), .rW1(id_ex_1_rwout), .rA(decoder_1_ra), .rB(decoder_1_rb),
    .RegWrite2(ex_mem_1_regwrite_2), .A_EX(A_EX), .A_MEM(A_MEM), .B_EX(B_EX), .B_MEM(B_MEM),
    .RegReadRA(not_3_out), .RegReadRB(not_4_out), .RegWrite1(id_ex_1_regwrite_2));
  Register #(.width(1)) register_3 (.D(and_15_out), .en(not_5_out), .Q(\暂停信号 ), .clk(clk), .clr(Go));
  and and_15 (and_15_out, syscall, ~show, ~equal);  // AND_Gate
  not not_5 (not_5_out, \暂停信号 );
  // Probe on decoder_1_pc
  and and_16 (and_16_out, syscall, equal);
  or or_8 (or_8_out, falsefetch, nop);
  and and_17 (falsej, predj, or_9_out, ~fly);  // AND_Gate
  and and_18 (and_18_out, ~predj, fly, or_9_out);  // AND_Gate
  or or_9 (or_9_out, w_j, w_b);
  or or_10 (or_10_out, and_16_out, ex_mem_1_stopout);
  or or_11 (Pause, nop, and_16_out, ex_mem_1_stopout, \暂停信号 );
  or or_12 (falsefetch, falsej, and_18_out);
  ID_EX id_ex_1 (
    .rA(registerfile_1_p7), .rB(registerfile_1_p8), .extend(decoder_1_extend), .ALUSrc(control_1_alusrc),
    .MemRead(control_1_memread), .MemWrite(control_1_memwrite), .RegWrite(control_1_regwrite),
    .NPC(if_id_1_npcout), .RW(decoder_1_rw), .rAout(id_ex_1_raout), .rBout(id_ex_1_rbout),
    .extendout(id_ex_1_extendout), .ALUSrcout(id_ex_1_alusrcout), .MemReadout(id_ex_1_memreadout),
    .MemWriteout(id_ex_1_memwriteout), .RegWrite_2(id_ex_1_regwrite_2), .NPCout(inAddr),
    .RWout(id_ex_1_rwout), .clk(clk), .RST(RST), .lh(control_1_lh), .lhout(id_ex_1_lhout),
    .ALUOP(control_1_aluop), .ALUOPout(id_ex_1_aluopout), .stop(or_10_out), .nop(or_8_out),
    .Jal(control_1_jal), .Jalout(Jal), .PC(decoder_1_pc), .PCout(id_ex_1_pcout), .jr(control_1_jr),
    .jrout(Jr), .jump(control_1_jump), .jumpout(Jump), .beq(control_1_beq), .beqout(beq),
    .bne(control_1_bne), .bneout(bne), .bgez(control_1_bgez), .bgezout(bgez), .syscallout(syscall),
    .syscall(control_1_syscall), .A_EX(A_EX), .A_EXout(id_ex_1_a_exout), .A_MEM(A_MEM),
    .A_MEMout(id_ex_1_a_memout), .B_EX(B_EX), .B_EXout(id_ex_1_b_exout), .B_MEM(B_MEM),
    .B_MEMout(id_ex_1_b_memout), .tCode(decoder_1_scode), .tCodeout(id_ex_1_tcodeout),
    .pred(if_id_1_predout), .predout(predj));
  // Probe on id_ex_1_pcout
  Multiplexer #(.width(32), .enable("false")) multiplexer_8 (
    .in0(id_ex_1_raout), .in1(multiplexer_14_out), .out(multiplexer_8_out), .sel(id_ex_1_a_memout));
  Multiplexer #(.width(32), .enable("false")) multiplexer_9 (
    .in0(id_ex_1_rbout), .in1(multiplexer_14_out), .out(multiplexer_9_out), .sel(id_ex_1_b_memout));
  Comparator #(.width(6), .mode("unsigned")) comparator_1 (
    .a(id_ex_1_tcodeout), .b(6'b100011), .eq(comparator_1_eq));  // open: gt, lt
  Comparator #(.width(6), .mode("unsigned")) comparator_2 (
    .a(id_ex_1_tcodeout), .b(6'b100001), .eq(comparator_2_eq));  // open: gt, lt
  Multiplexer #(.width(32), .enable("false")) multiplexer_10 (
    .in0(multiplexer_8_out), .in1(alu_1_p7), .out(multiplexer_10_out), .sel(id_ex_1_a_exout));
  Multiplexer #(.width(32), .enable("false")) multiplexer_11 (
    .in0(multiplexer_9_out), .in1(alu_1_p7), .out(multiplexer_11_out), .sel(id_ex_1_b_exout));
  and and_19 (and_19_out, syscall, equal);
  or or_13 (or_13_out, comparator_1_eq, comparator_2_eq);
  not not_6 (cmp, comparator_3_gt);
  Comparator #(.width(32)) comparator_3 (.a({32{1'b0}}), .b(multiplexer_10_out), .gt(comparator_3_gt));  // open: eq, lt
  Comparator #(.width(32), .mode("unsigned")) comparator_4 (
    .a(multiplexer_10_out), .b(32'h22), .eq(show));  // open: gt, lt
  Comparator #(.width(32), .mode("unsigned")) comparator_5 (
    .a(multiplexer_10_out), .b(32'ha), .eq(equal));  // open: gt, lt
  Shifter #(.width(32)) shifter_1 (.in(id_ex_1_extendout), .\dist (5'b00010), .out(shifter_1_out));
  // Probe on nothing
  Multiplexer #(.width(32), .enable("false")) multiplexer_12 (
    .in0(multiplexer_11_out), .in1(id_ex_1_extendout), .out(multiplexer_12_out), .sel(id_ex_1_alusrcout));
  and and_20 (and_20_out, show, syscall);
  and and_21 (nop, or_13_out, or_14_out);
  or or_14 (or_14_out, A_EX, B_EX);
  Adder #(.width(32)) adder_3 (.a(inAddr), .b(shifter_1_out), .out(baddr));  // open: cin, cout
  // ALU alu_1: pin names not known; wires that end beside it: multiplexer_10_out, multiplexer_12_out, id_ex_1_aluopout, Bequal, alu_1_p5, alu_1_p6, alu_1_p7, alu_1_p7[21:2]
  Register #(.width(32)) register_4 (.D(multiplexer_12_out), .en(and_20_out), .Q(SyscallOut), .clk(clk), .clr(RST));
  // Probe on alu_1_p5
  EX_MEM ex_mem_1 (
    .NPC(inAddr), .ALURes(alu_1_p6), .rB(multiplexer_11_out), .MemWrite(id_ex_1_memwriteout),
    .MemRead(id_ex_1_memreadout), .lh(id_ex_1_lhout), .rW(id_ex_1_rwout), .NPCout(ex_mem_1_npcout),
    .ALUout(alu_1_p7), .rBout(ex_mem_1_rbout), .MemWrite_2(ex_mem_1_memwrite_2),
    .MemRead_2(ex_mem_1_memread_2), .lh_2(ex_mem_1_lh_2), .rWout(ex_mem_1_rwout), .clk(clk), .rst(RST),
    .RegWrite(id_ex_1_regwrite_2), .RegWrite_2(ex_mem_1_regwrite_2), .Stop(and_19_out),
    .Stopout(ex_mem_1_stopout), .stop_2(or_15_out), .Jal(Jal), .Jalout(ex_mem_1_jalout));
  or or_15 (or_15_out, \暂停信号 , ex_mem_1_stopout);
  // Probe on ex_mem_1_rbout
  // Probe on multiplexer_14_out
  Multiplexer #(.width(32), .enable("false")) multiplexer_13 (
    .in0(alu_1_p7), .in1(mips_ram_1_p7), .out(multiplexer_13_out), .sel(ex_mem_1_memread_2));
  // MIPS_RAM mips_ram_1: pin names not known; wires that end beside it: alu_1_p7[21:2], ex_mem_1_rbout, ex_mem_1_memwrite_2, clk, ex_mem_1_memread_2, RST, mips_ram_1_p7
  or or_16 (or_16_out, \暂停信号 , mem_wb_1_stopout);
  // Probe on multiplexer_14_out
  MEM_WB mem_wb_1 (
    .NPC(ex_mem_1_npcout), .DR(multiplexer_13_out), .rW(ex_mem_1_rwout), .lh(ex_mem_1_lh_2),
    .RegWrite(ex_mem_1_regwrite_2), .Stopin(ex_mem_1_stopout), .NPCout(NPC), .DRout(mem_wb_1_drout),
    .rWout(rW), .lhout(lh), .RegWriteout(RegWrite), .Stopout(mem_wb_1_stopout), .clk(clk), .rst(RST),
    .stop(or_16_out), .Jal(ex_mem_1_jalout), .Jalout(jal_t));
  Multiplexer #(.width(32), .enable("false")) multiplexer_14 (
    .in0(mem_wb_1_drout), .in1({multiplexer_15_out, mem_wb_1_drout[15:0]}), .out(multiplexer_14_out), .sel(lh));
  Register #(.width(1)) register_5 (.D(mem_wb_1_stopout), .Q(stop), .clk(clk), .clr(RST));  // open: en
  Multiplexer #(.width(16), .enable("false")) multiplexer_15 (
    .in0({16{1'b0}}), .in1({16{1'b1}}), .out(multiplexer_15_out), .sel(mem_wb_1_drout[15]));
  Multiplexer #(.width(32), .enable("false")) multiplexer_16 (
    .in0(multiplexer_14_out), .in1(NPC), .out(writeData), .sel(jal_t));
  Pull_Resistor pull_resistor_1 (.node(mem_wb_1_drout[15]));

  // Notes on the sheet:
  //   中断源
  //   中断请求指示
  //   指令存储器
  //   contents of rom_1 (hex, n*v repeats v):
  //   20110001 8000005 20110001 20120002 20130003 8000009 20110001 20120002 20130003 800000d 20110001
  //   20120002 20130003 8000011 20110001 20120002 20130003 c0000f6 20100001 20110001 118fc0 112020
  //   20020022 c 118882 12200001 8000015 112020 20020022 c 20110001 118880 112020 20020022 c 12200001
  //   800001f 20110001 118fc0 112020 20020022 c 1188c3 112020 20020022 c 118903 112020 20020022 c 118903
  //   112020 20020022 c 118903 112020 20020022 c 118903 112020 20020022 c 118903 112020 20020022 c 118903
  //   112020 20020022 c 118903 112020 20020022 c 20100001 109fc0 139fc3 8021 2012000c 24160003 26100001
  //   3210000f 20080008 20090001 139900 2709825 132020 20020022 c 1094022 1500fff9 22100001 2018000f
  //   2188024 108700 20080008 20090001 139902 2709825 132021 20020022 c 1094022 1500fff9 108702 2c9b022
  //   12c00001 8000050 4020 1084027 84400 3508ffff 82021 20020022 c 2010ffff 20110000 ae300000 22100001
  //   22310004 ae300000 22100001 22310004 ae300000 22100001 22310004 ae300000 22100001 22310004 ae300000
  //   22100001 22310004 ae300000 22100001 22310004 ae300000 22100001 22310004 ae300000 22100001 22310004
  //   ae300000 22100001 22310004 ae300000 22100001 22310004 ae300000 22100001 22310004 ae300000 22100001
  //   22310004 ae300000 22100001 22310004 ae300000 22100001 22310004 ae300000 22100001 22310004 ae300000
  //   22100001 22310004 22100001 8020 2011003c 8e130000 8e340000 274402a 11000002 ae330000 ae140000
  //   2231fffc 1611fff8 102020 20020022 c 22100004 2011003c 1611fff2 20020032 c 0 0 20080001 20110010
  //   112020 20020022 c 200b0020 2288823 112020 20020022 c 216bffff 1560fffa 0 0 2008ffff 20117777 112020
  //   20020022 c 200b0010 3a31ffff 112020 20020022 c 216bffff 1560fffa 0 0 20090000 200b0010 34118483
  //   20120404 118c00 129400 36318281 22520404 ad310000 2328820 21290004 216bffff 1560fffb 200b0020
  //   20090000 85310000 112020 20020022 c 21290002 216bffff 1560fff9 0 0 2011000f 112020 20020022 c
  //   2231ffff 621fffb 2002000a c 20100000 22100001 102020 20020022 c 22100002 102020 20020022 c 22100003
  //   102020 20020022 c 22100004 102020 20020022 c 22100005 102020 20020022 c 22100006 102020 20020022 c
  //   22100007 102020 20020022 c 22100008 102020 20020022 20020022 c 3e00008
  //   寄存器文件
endmodule

module Control (
  input  [5:0] OPCODE,
  input  [5:0] FUNCT,
  output [3:0] ALUOP,
  output MemRead,
  output shift,
  output ALUSrc,
  output Zero_extend,
  output RegDst,
  output Jump,
  output RegWrite,
  output beq,
  output bne,
  output MemWrite,
  output Jal,
  output jr,
  output syscall,
  output RegReadRB,
  output bgez,
  output lh
);

  wire add, addi, addiu, addu, \and , andi, comparator_1_eq, comparator_16_eq, comparator_17_eq,
       comparator_18_eq, comparator_19_eq, comparator_20_eq, comparator_21_eq, comparator_22_eq,
       comparator_23_eq, comparator_24_eq, comparator_25_eq, comparator_26_eq, comparator_27_eq,
       comparator_28_eq, comparator_29_eq, j, lw, \nor , \or , or_1_out, or_2_out, or_3_out, or_4_out,
       or_10_out, ori, sll, slt, slti, sltu, sra, srl, sub, subu, xori;

  Comparator #(.width(6)) comparator_1 (.a(OPCODE), .b({6{1'b0}}), .eq(comparator_1_eq));  // open: gt, lt
  Comparator #(.width(6)) comparator_2 (.a(OPCODE), .b(6'b001000), .eq(addi));  // open: gt, lt
  Comparator #(.width(6)) comparator_3 (.a(OPCODE), .b(6'b001001), .eq(addiu));  // open: gt, lt
  Comparator #(.width(6)) comparator_4 (.a(OPCODE), .b(6'b001100), .eq(andi));  // open: gt, lt
  Comparator #(.width(6)) comparator_5 (.a(OPCODE), .b(6'b001101), .eq(ori));  // open: gt, lt
  Comparator #(.width(6)) comparator_6 (.a(OPCODE), .b(6'b100011), .eq(lw));  // open: gt, lt
  Comparator #(.width(6)) comparator_7 (.a(OPCODE), .b(6'b101011), .eq(MemWrite));  // open: gt, lt
  Comparator #(.width(6)) comparator_8 (.a(OPCODE), .b(6'b000100), .eq(beq));  // open: gt, lt
  Comparator #(.width(6)) comparator_9 (.a(OPCODE), .b(6'b000101), .eq(bne));  // open: gt, lt
  Comparator #(.width(6)) comparator_10 (.a(OPCODE), .b(6'b001010), .eq(slti));  // open: gt, lt
  Comparator #(.width(6)) comparator_11 (.a(OPCODE), .b(6'b000010), .eq(j));  // open: gt, lt
  Comparator #(.width(6)) comparator_12 (.a(OPCODE), .b(6'b000011), .eq(Jal));  // open: gt, lt
  Comparator #(.width(6)) comparator_13 (.a(OPCODE), .b(6'b001110), .eq(xori));  // open: gt, lt
  Comparator #(.width(6)) comparator_14 (.a(OPCODE), .b(6'b100001), .eq(lh));  // open: gt, lt
  Comparator #(.width(6)) comparator_15 (.a(OPCODE), .b(6'b000001), .eq(bgez));  // open: gt, lt
  Comparator #(.width(6)) comparator_16 (.a(FUNCT), .b(6'b100000), .eq(comparator_16_eq));  // open: gt, lt
  Comparator #(.width(6)) comparator_17 (.a(FUNCT), .b(6'b100001), .eq(comparator_17_eq));  // open: gt, lt
  Comparator #(.width(6)) comparator_18 (.a(FUNCT), .b(6'b100100), .eq(comparator_18_eq));  // open: gt, lt
  Comparator #(.width(6)) comparator_19 (.a(FUNCT), .b({6{1'b0}}), .eq(comparator_19_eq));  // open: gt, lt
  Comparator #(.width(6)) comparator_20 (.a(FUNCT), .b(6'b000011), .eq(comparator_20_eq));  // open: gt, lt
  Comparator #(.width(6)) comparator_21 (.a(FUNCT), .b(6'b000010), .eq(comparator_21_eq));  // open: gt, lt
  Comparator #(.width(6)) comparator_22 (.a(FUNCT), .b(6'b100010), .eq(comparator_22_eq));  // open: gt, lt
  Comparator #(.width(6)) comparator_23 (.a(FUNCT), .b(6'b100101), .eq(comparator_23_eq));  // open: gt, lt
  Comparator #(.width(6)) comparator_24 (.a(FUNCT), .b(6'b100111), .eq(comparator_24_eq));  // open: gt, lt
  Comparator #(.width(6)) comparator_25 (.a(FUNCT), .b(6'b101010), .eq(comparator_25_eq));  // open: gt, lt
  Comparator #(.width(6)) comparator_26 (.a(FUNCT), .b(6'b101011), .eq(comparator_26_eq));  // open: gt, lt
  Comparator #(.width(6)) comparator_27 (.a(FUNCT), .b(6'b001000), .eq(comparator_27_eq));  // open: gt, lt
  Comparator #(.width(6)) comparator_28 (.a(FUNCT), .b(6'b001100), .eq(comparator_28_eq));  // open: gt, lt
  Comparator #(.width(6)) comparator_29 (.a(FUNCT), .b(6'b100011), .eq(comparator_29_eq));  // open: gt, lt
  and and_1 (add, comparator_1_eq, comparator_16_eq);
  and and_2 (addu, comparator_1_eq, comparator_17_eq);
  and and_3 (\and , comparator_1_eq, comparator_18_eq);
  and and_4 (sll, comparator_1_eq, comparator_19_eq);
  and and_5 (sra, comparator_1_eq, comparator_20_eq);
  and and_6 (srl, comparator_1_eq, comparator_21_eq);
  and and_7 (sub, comparator_1_eq, comparator_22_eq);
  and and_8 (\or , comparator_1_eq, comparator_23_eq);
  and and_9 (\nor , comparator_1_eq, comparator_24_eq);
  and and_10 (slt, comparator_1_eq, comparator_25_eq);
  and and_11 (sltu, comparator_1_eq, comparator_26_eq);
  and and_12 (jr, comparator_1_eq, comparator_27_eq);
  and and_13 (syscall, comparator_1_eq, comparator_28_eq);
  and and_14 (subu, comparator_1_eq, comparator_29_eq);
  or or_1 (or_1_out, sub, subu);
  or or_2 (or_2_out, \and , andi);
  or or_3 (or_3_out, \or , ori);
  or or_4 (or_4_out, slt, slti);
  or or_5 (MemRead, lw, lh);
  or or_6 (shift, sll, sra, srl);
  or or_7 (Zero_extend, xori, andi, ori);
  or or_8 (RegDst, add, \nor , addu, \and , sll, sra, srl, \or , slt, sltu, subu, sub);
  or or_9 (Jump, j, Jal);
  or or_10 (or_10_out, add, addi, addiu, addu, lw, MemWrite, beq, bne, bgez, lh);
  Priority_Encoder #(.select(4)) priority_encoder_1 (
    .in0(sll), .in1(sra), .in2(srl), .in3(1'b0), .in4(1'b0), .in5(or_10_out), .in6(or_1_out), .in7(or_2_out),
    .in8(or_3_out), .in9(xori), .in10(\nor ), .in11(or_4_out), .in12(sltu), .in13(1'b0), .in14(1'b0),
    .in15(1'b0), .out(ALUOP));  // open: gs, en_out, en_in
  or or_11 (ALUSrc, addi, addiu, andi, sll, sra, srl, ori, lw, MemWrite, slti, xori, lh);
  or or_12 (RegWrite, slt, add, addiu, addu, \and , sll, sra, \nor , srl, \or , lh, sltu, subu, sub, addi, andi, ori, lw, slti, xori, Jal);
  or or_13 (RegReadRB, addi, addiu, andi, sll, sra, srl, ori, lw, xori, slti, lh, j, jr, Jal, bgez);

  // Other names for the same wires on the sheet: sw = MemWrite
endmodule

module Decoder (
  input  [31:0] CODE,
  input  shift,
  input  syscall,
  input  RegDst,
  input  Jal,
  input  Zero_extend,
  output [27:0] PC,
  output [5:0] OPCODE,
  output [5:0] FUNCT,
  output [5:0] sCODE,
  output [4:0] RA,
  output [4:0] RB,
  output [4:0] RW,
  output [31:0] extend
);

  wire [4:0] multiplexer_1_out, multiplexer_2_out;
  wire [31:0] bit_extender_1_out, bit_extender_2_out, bit_extender_3_out, multiplexer_6_out;

  Shifter #(.width(28)) shifter_1 (.in(CODE[27:0]), .\dist (5'b00010), .out(PC));
  Multiplexer #(.width(5), .enable("false")) multiplexer_1 (
    .in0(CODE[25:21]), .in1(CODE[20:16]), .out(multiplexer_1_out), .sel(shift));
  Multiplexer #(.width(5), .enable("false")) multiplexer_2 (
    .in0(CODE[20:16]), .in1(CODE[15:11]), .out(multiplexer_2_out), .sel(RegDst));
  // Probe on CODE[15:0]
  Multiplexer #(.width(5), .enable("false")) multiplexer_3 (
    .in0(multiplexer_1_out), .in1(5'b00010), .out(RA), .sel(syscall));
  Multiplexer #(.width(5), .enable("false")) multiplexer_4 (
    .in0(multiplexer_2_out), .in1({5{1'b1}}), .out(RW), .sel(Jal));
  assign bit_extender_1_out = {{16{CODE[15]}}, CODE[15:0]};  // Bit_Extender bit_extender_1
  assign bit_extender_2_out = {{16{1'b0}}, CODE[15:0]};  // Bit_Extender bit_extender_2
  assign bit_extender_3_out = {{27{1'b0}}, CODE[10:6]};  // Bit_Extender bit_extender_3
  Multiplexer #(.width(5), .enable("false")) multiplexer_5 (.in0(CODE[20:16]), .in1(5'b00100), .out(RB), .sel(syscall));
  Multiplexer #(.width(32), .enable("false")) multiplexer_6 (
    .in0(bit_extender_1_out), .in1(bit_extender_2_out), .out(multiplexer_6_out), .sel(Zero_extend));
  // Probe on bit_extender_3_out
  Multiplexer #(.width(32), .enable("false")) multiplexer_7 (
    .in0(multiplexer_6_out), .in1(bit_extender_3_out), .out(extend), .sel(shift));

  assign FUNCT = CODE[5:0];
  assign OPCODE = CODE[31:26];
  assign sCODE = CODE[31:26];
endmodule

module IF_ID (
  input  pause,
  input  [31:0] NPC,
  input  [31:0] IR,
  input  pred,
  input  branch,
  input  clk,
  input  RST,
  output [31:0] NPCout,
  output [31:0] IRout,
  output predout
);

  wire multiplexer_3_out, not_1_out;
  wire [31:0] multiplexer_1_out, multiplexer_2_out;

  Multiplexer #(.width(32), .enable("false")) multiplexer_1 (
    .in0(NPC), .in1({32{1'b0}}), .out(multiplexer_1_out), .sel(branch));
  Multiplexer #(.width(32), .enable("false")) multiplexer_2 (
    .in0(IR), .in1({32{1'b0}}), .out(multiplexer_2_out), .sel(branch));
  Multiplexer #(.enable("false")) multiplexer_3 (.in0(pred), .in1(1'b0), .out(multiplexer_3_out), .sel(branch));
  not not_1 (not_1_out, pause);
  Register #(.width(32)) u_NPC (.D(multiplexer_1_out), .en(not_1_out), .Q(NPCout), .clk(clk), .clr(RST));
  Register #(.width(32)) u_IR (.D(multiplexer_2_out), .en(not_1_out), .Q(IRout), .clk(clk), .clr(RST));
  Register #(.width(1)) register_1 (.D(multiplexer_3_out), .en(not_1_out), .Q(predout), .clk(clk), .clr(RST));
endmodule

module ID_EX (
  input  nop,
  input  [31:0] rA,
  input  [31:0] rB,
  input  [31:0] extend,
  input  ALUSrc,
  input  MemRead,
  input  MemWrite,
  input  RegWrite,
  input  lh,
  input  [3:0] ALUOP,
  input  Jal,
  input  [31:0] NPC,
  input  [4:0] RW,
  input  [27:0] PC,
  input  jr,
  input  jump,
  input  beq,
  input  bne,
  input  bgez,
  input  syscall,
  input  A_EX,
  input  A_MEM,
  input  B_EX,
  input  B_MEM,
  input  [5:0] tCode,
  input  pred,
  input  clk,
  input  RST,
  input  stop,
  output [31:0] rAout,
  output [31:0] rBout,
  output [31:0] extendout,
  output ALUSrcout,
  output MemReadout,
  output MemWriteout,
  output RegWrite_2,
  output lhout,
  output [3:0] ALUOPout,
  output Jalout,
  output [31:0] NPCout,
  output [4:0] RWout,
  output [27:0] PCout,
  output jrout,
  output jumpout,
  output beqout,
  output bneout,
  output bgezout,
  output syscallout,
  output A_EXout,
  output A_MEMout,
  output B_EXout,
  output B_MEMout,
  output [5:0] tCodeout,
  output predout
);

  wire multiplexer_4_out, multiplexer_5_out, multiplexer_6_out, multiplexer_7_out, multiplexer_8_out,
       multiplexer_10_out, multiplexer_14_out, multiplexer_15_out, multiplexer_16_out, multiplexer_17_out,
       multiplexer_18_out, multiplexer_19_out, multiplexer_20_out, multiplexer_21_out, multiplexer_22_out,
       multiplexer_23_out, multiplexer_25_out, not_1_out;
  wire [3:0] multiplexer_9_out;
  wire [4:0] multiplexer_12_out;
  wire [5:0] multiplexer_24_out;
  wire [27:0] multiplexer_13_out;
  wire [31:0] multiplexer_1_out, multiplexer_2_out, multiplexer_3_out, multiplexer_11_out;

  Multiplexer #(.width(32), .enable("false")) multiplexer_1 (
    .in0(rA), .in1({32{1'b0}}), .out(multiplexer_1_out), .sel(nop));
  Multiplexer #(.width(32), .enable("false")) multiplexer_2 (
    .in0(rB), .in1({32{1'b0}}), .out(multiplexer_2_out), .sel(nop));
  Multiplexer #(.width(32), .enable("false")) multiplexer_3 (
    .in0(extend), .in1({32{1'b0}}), .out(multiplexer_3_out), .sel(nop));
  Multiplexer #(.enable("false")) multiplexer_4 (.in0(ALUSrc), .in1(1'b0), .out(multiplexer_4_out), .sel(nop));
  Multiplexer #(.enable("false")) multiplexer_5 (.in0(MemRead), .in1(1'b0), .out(multiplexer_5_out), .sel(nop));
  Multiplexer #(.enable("false")) multiplexer_6 (.in0(MemWrite), .in1(1'b0), .out(multiplexer_6_out), .sel(nop));
  Multiplexer #(.enable("false")) multiplexer_7 (.in0(RegWrite), .in1(1'b0), .out(multiplexer_7_out), .sel(nop));
  Multiplexer #(.enable("false")) multiplexer_8 (.in0(lh), .in1(1'b0), .out(multiplexer_8_out), .sel(nop));
  Multiplexer #(.width(4), .enable("false")) multiplexer_9 (
    .in0(ALUOP), .in1(4'b0000), .out(multiplexer_9_out), .sel(nop));
  Multiplexer #(.enable("false")) multiplexer_10 (.in0(Jal), .in1(1'b0), .out(multiplexer_10_out), .sel(nop));
  Multiplexer #(.width(32), .enable("false")) multiplexer_11 (
    .in0(NPC), .in1({32{1'b0}}), .out(multiplexer_11_out), .sel(nop));
  Multiplexer #(.width(5), .enable("false")) multiplexer_12 (
    .in0(RW), .in1({5{1'b0}}), .out(multiplexer_12_out), .sel(nop));
  Multiplexer #(.width(28), .enable("false")) multiplexer_13 (
    .in0(PC), .in1({28{1'b0}}), .out(multiplexer_13_out), .sel(nop));
  Multiplexer #(.enable("false")) multiplexer_14 (.in0(jr), .in1(1'b0), .out(multiplexer_14_out), .sel(nop));
  Multiplexer #(.enable("false")) multiplexer_15 (.in0(jump), .in1(1'b0), .out(multiplexer_15_out), .sel(nop));
  Multiplexer #(.enable("false")) multiplexer_16 (.in0(beq), .in1(1'b0), .out(multiplexer_16_out), .sel(nop));
  Multiplexer #(.enable("false")) multiplexer_17 (.in0(bne), .in1(1'b0), .out(multiplexer_17_out), .sel(nop));
  Multiplexer #(.enable("false")) multiplexer_18 (.in0(bgez), .in1(1'b0), .out(multiplexer_18_out), .sel(nop));
  Multiplexer #(.enable("false")) multiplexer_19 (.in0(syscall), .in1(1'b0), .out(multiplexer_19_out), .sel(nop));
  Multiplexer #(.enable("false")) multiplexer_20 (.in0(A_EX), .in1(1'b0), .out(multiplexer_20_out), .sel(nop));
  Multiplexer #(.enable("false")) multiplexer_21 (.in0(A_MEM), .in1(1'b0), .out(multiplexer_21_out), .sel(nop));
  Multiplexer #(.enable("false")) multiplexer_22 (.in0(B_EX), .in1(1'b0), .out(multiplexer_22_out), .sel(nop));
  Multiplexer #(.enable("false")) multiplexer_23 (.in0(B_MEM), .in1(1'b0), .out(multiplexer_23_out), .sel(nop));
  Multiplexer #(.width(6), .enable("false")) multiplexer_24 (
    .in0(tCode), .in1({6{1'b0}}), .out(multiplexer_24_out), .sel(nop));
  Multiplexer #(.enable("false")) multiplexer_25 (.in0(pred), .in1(1'b0), .out(multiplexer_25_out), .sel(nop));
  not not_1 (not_1_out, stop);
  Register #(.width(32)) register_1 (.D(multiplexer_1_out), .en(not_1_out), .Q(rAout), .clk(clk), .clr(RST));
  Register #(.width(32)) register_2 (.D(multiplexer_2_out), .en(not_1_out), .Q(rBout), .clk(clk), .clr(RST));
  Register #(.width(32)) register_3 (.D(multiplexer_3_out), .en(not_1_out), .Q(extendout), .clk(clk), .clr(RST));
  Register #(.width(1)) register_4 (.D(multiplexer_4_out), .en(not_1_out), .Q(ALUSrcout), .clk(clk), .clr(RST));
  Register #(.width(1)) register_5 (.D(multiplexer_5_out), .en(not_1_out), .Q(MemReadout), .clk(clk), .clr(RST));
  Register #(.width(1)) register_6 (.D(multiplexer_6_out), .en(not_1_out), .Q(MemWriteout), .clk(clk), .clr(RST));
  Register #(.width(1)) register_7 (.D(multiplexer_7_out), .en(not_1_out), .Q(RegWrite_2), .clk(clk), .clr(RST));
  Register #(.width(1)) register_8 (.D(multiplexer_8_out), .en(not_1_out), .Q(lhout), .clk(clk), .clr(RST));
  Register #(.width(4)) register_9 (.D(multiplexer_9_out), .en(not_1_out), .Q(ALUOPout), .clk(clk), .clr(RST));
  Register #(.width(1)) register_10 (.D(multiplexer_10_out), .en(not_1_out), .Q(Jalout), .clk(clk), .clr(RST));
  Register #(.width(32)) register_11 (.D(multiplexer_11_out), .en(not_1_out), .Q(NPCout), .clk(clk), .clr(RST));
  Register #(.width(5)) register_12 (.D(multiplexer_12_out), .en(not_1_out), .Q(RWout), .clk(clk), .clr(RST));
  Register #(.width(28)) register_13 (.D(multiplexer_13_out), .en(not_1_out), .Q(PCout), .clk(clk), .clr(RST));
  Register #(.width(1)) register_14 (.D(multiplexer_14_out), .en(not_1_out), .Q(jrout), .clk(clk), .clr(RST));
  Register #(.width(1)) register_15 (.D(multiplexer_15_out), .en(not_1_out), .Q(jumpout), .clk(clk), .clr(RST));
  Register #(.width(1)) register_16 (.D(multiplexer_16_out), .en(not_1_out), .Q(beqout), .clk(clk), .clr(RST));
  Register #(.width(1)) register_17 (.D(multiplexer_17_out), .en(not_1_out), .Q(bneout), .clk(clk), .clr(RST));
  Register #(.width(1)) register_18 (.D(multiplexer_18_out), .en(not_1_out), .Q(bgezout), .clk(clk), .clr(RST));
  Register #(.width(1)) register_19 (.D(multiplexer_19_out), .en(not_1_out), .Q(syscallout), .clk(clk), .clr(RST));
  Register #(.width(1)) register_20 (.D(multiplexer_20_out), .en(not_1_out), .Q(A_EXout), .clk(clk), .clr(RST));
  Register #(.width(1)) register_21 (.D(multiplexer_21_out), .en(not_1_out), .Q(A_MEMout), .clk(clk), .clr(RST));
  Register #(.width(1)) register_22 (.D(multiplexer_22_out), .en(not_1_out), .Q(B_EXout), .clk(clk), .clr(RST));
  Register #(.width(1)) register_23 (.D(multiplexer_23_out), .en(not_1_out), .Q(B_MEMout), .clk(clk), .clr(RST));
  Register #(.width(6)) register_24 (.D(multiplexer_24_out), .en(not_1_out), .Q(tCodeout), .clk(clk), .clr(RST));
  Register #(.width(1)) register_25 (.D(multiplexer_25_out), .en(not_1_out), .Q(predout), .clk(clk), .clr(RST));
endmodule

module EX_MEM (
  input  [31:0] NPC,
  input  [31:0] ALURes,
  input  [31:0] rB,
  input  MemWrite,
  input  MemRead,
  input  lh,
  input  [4:0] rW,
  input  RegWrite,
  input  Stop,
  input  Jal,
  input  clk,
  input  rst,
  input  stop_2,
  output [31:0] NPCout,
  output [31:0] ALUout,
  output [31:0] rBout,
  output MemWrite_2,
  output MemRead_2,
  output lh_2,
  output [4:0] rWout,
  output RegWrite_2,
  output Stopout,
  output Jalout
);

  wire not_1_out;

  not not_1 (not_1_out, stop_2);
  Register #(.width(32)) register_1 (.D(NPC), .en(not_1_out), .Q(NPCout), .clk(clk), .clr(rst));
  Register #(.width(32)) register_2 (.D(ALURes), .en(not_1_out), .Q(ALUout), .clk(clk), .clr(rst));
  Register #(.width(32)) register_3 (.D(rB), .en(not_1_out), .Q(rBout), .clk(clk), .clr(rst));
  Register #(.width(1)) register_4 (.D(MemWrite), .en(not_1_out), .Q(MemWrite_2), .clk(clk), .clr(rst));
  Register #(.width(1)) register_5 (.D(MemRead), .en(not_1_out), .Q(MemRead_2), .clk(clk), .clr(rst));
  Register #(.width(1)) register_6 (.D(lh), .en(not_1_out), .Q(lh_2), .clk(clk), .clr(rst));
  Register #(.width(5)) register_7 (.D(rW), .en(not_1_out), .Q(rWout), .clk(clk), .clr(rst));
  Register #(.width(1)) register_8 (.D(RegWrite), .en(not_1_out), .Q(RegWrite_2), .clk(clk), .clr(rst));
  Register #(.width(1)) register_9 (.D(Stop), .en(not_1_out), .Q(Stopout), .clk(clk), .clr(rst));
  Register #(.width(1)) register_10 (.D(Jal), .en(not_1_out), .Q(Jalout), .clk(clk), .clr(rst));
endmodule

module MEM_WB (
  input  [31:0] NPC,
  input  [31:0] DR,
  input  [4:0] rW,
  input  lh,
  input  RegWrite,
  input  Stopin,
  input  Jal,
  input  clk,
  input  rst,
  input  stop,
  output [31:0] NPCout,
  output [31:0] DRout,
  output [4:0] rWout,
  output lhout,
  output RegWriteout,
  output Stopout,
  output Jalout
);

  wire not_1_out;

  not not_1 (not_1_out, stop);
  Register #(.width(32)) register_1 (.D(NPC), .en(not_1_out), .Q(NPCout), .clk(clk), .clr(rst));
  Register #(.width(32)) register_2 (.D(DR), .en(not_1_out), .Q(DRout), .clk(clk), .clr(rst));
  Register #(.width(5)) register_3 (.D(rW), .en(not_1_out), .Q(rWout), .clk(clk), .clr(rst));
  Register #(.width(1)) register_4 (.D(lh), .en(not_1_out), .Q(lhout), .clk(clk), .clr(rst));
  Register #(.width(1)) register_5 (.D(RegWrite), .en(not_1_out), .Q(RegWriteout), .clk(clk), .clr(rst));
  Register #(.width(1)) register_6 (.D(Stopin), .en(not_1_out), .Q(Stopout), .clk(clk), .clr(rst));
  Register #(.width(1)) register_7 (.D(Jal), .en(not_1_out), .Q(Jalout), .clk(clk), .clr(rst));
endmodule

module nop (
  input  [4:0] rA,
  input  [4:0] rB,
  input  [4:0] rW1,
  input  [4:0] rW2,
  input  RegWrite1,
  input  RegWrite2,
  input  RegReadRA,
  input  RegReadRB,
  output B_EX,
  output B_MEM,
  output A_MEM,
  output A_EX
);

  wire comparator_1_eq, comparator_2_eq, comparator_3_eq, comparator_4_eq, comparator_5_eq, comparator_6_eq,
       not_1_out, not_2_out;

  Comparator #(.width(5), .mode("unsigned")) comparator_1 (.a(rA), .b(rW1), .eq(comparator_1_eq));  // open: gt, lt
  Comparator #(.width(5), .mode("unsigned")) comparator_2 (.a(rA), .b(rW2), .eq(comparator_2_eq));  // open: gt, lt
  not not_1 (not_1_out, comparator_3_eq);
  Comparator #(.width(5), .mode("unsigned")) comparator_3 (
    .a(rA), .b({5{1'b0}}), .eq(comparator_3_eq));  // open: gt, lt
  and and_1 (A_MEM, RegReadRA, RegWrite2, comparator_2_eq, not_1_out);
  and and_2 (A_EX, RegReadRA, RegWrite1, comparator_1_eq, not_1_out);
  not not_2 (not_2_out, comparator_4_eq);
  Comparator #(.width(5), .mode("unsigned")) comparator_4 (
    .a(rB), .b({5{1'b0}}), .eq(comparator_4_eq));  // open: gt, lt
  Comparator #(.width(5), .mode("unsigned")) comparator_5 (.a(rB), .b(rW1), .eq(comparator_5_eq));  // open: gt, lt
  Comparator #(.width(5), .mode("unsigned")) comparator_6 (.a(rB), .b(rW2), .eq(comparator_6_eq));  // open: gt, lt
  and and_3 (B_MEM, RegReadRB, RegWrite2, comparator_6_eq, not_2_out);
  and and_4 (B_EX, RegReadRB, RegWrite1, comparator_5_eq, not_2_out);
endmodule

module \预测状态跳转  (
  input  Suc,
  input  [1:0] preState,
  output [1:0] nextState
);

  wire _00_out, _01_out, _10_out, _11_out, and_1_out, and_2_out, and_3_out, and_4_out, and_5_out, and_6_out,
       and_7_out, and_8_out, or_1_out, or_2_out;

  and _00 (_00_out, ~preState[0], ~preState[1]);  // AND_Gate
  and _01 (_01_out, preState[0], ~preState[1]);  // AND_Gate
  and _10 (_10_out, ~preState[0], preState[1]);  // AND_Gate
  and _11 (_11_out, preState[0], preState[1]);
  and and_1 (and_1_out, Suc, _00_out);
  and and_2 (and_2_out, ~Suc, _00_out);  // AND_Gate
  and and_3 (and_3_out, Suc, _01_out);
  and and_4 (and_4_out, ~Suc, _01_out);  // AND_Gate
  and and_5 (and_5_out, Suc, _10_out);
  and and_6 (and_6_out, ~Suc, _10_out);  // AND_Gate
  and and_7 (and_7_out, Suc, _11_out);
  and and_8 (and_8_out, ~Suc, _11_out);  // AND_Gate
  or or_1 (or_1_out, and_2_out, and_4_out, and_6_out);
  or or_2 (or_2_out, and_3_out, and_5_out, and_7_out);
  Priority_Encoder #(.select(2)) priority_encoder_1 (
    .in0(or_1_out), .in1(and_1_out), .in2(and_8_out), .in3(or_2_out), .out(nextState));  // open: gs, en_out, en_in

  // Notes on the sheet:
  //   01
  //   00
  //   11
  //   00
  //   11
  //   00
  //   11
  //   10
endmodule

module BHT (
  input  [31:0] nextAddr,
  input  [31:0] inAddr,
  input  success,
  input  w_b,
  input  w_j,
  input  clk,
  input  [31:0] searchAddr,
  output [31:0] targetAddr,
  output [1:0] nextState,
  output hit
);

  wire and_1_out, and_2_out, and_3_out, and_4_out, and_5_out, and_6_out, and_7_out, and_8_out, and_9_out,
       and_10_out, and_11_out, and_12_out, comparator_1_eq, comparator_2_eq, comparator_3_eq,
       comparator_4_eq, comparator_5_eq, comparator_6_eq, comparator_7_eq, comparator_8_eq, comparator_9_lt,
       comparator_10_lt, comparator_11_lt, demultiplexer_1_out0, demultiplexer_1_out1, demultiplexer_1_out2,
       demultiplexer_1_out3, newRecord, not_1_out, not_2_out, not_3_out, not_4_out, not_6_out,
       priority_encoder_2_gs, priority_encoder_3_en_out, valid1, valid2, valid3, valid4, write;
  wire [1:0] multiplexer_2_out, multiplexer_3_out, multiplexer_4_out, multiplexer_5_out, multiplexer_6_out,
       multiplexer_7_out, not_5_out, priority_encoder_2_out, priority_encoder_3_out, priority_encoder_4_out,
       register_13_q, register_14_q, register_15_q, register_16_q, Sel, \预测状态跳转_1_nextstate ,
       \预测状态跳转_2_nextstate , \预测状态跳转_3_nextstate , \预测状态跳转_4_nextstate ;
  wire [9:0] addr1, addr2, addr3, addr4;
  wire [15:0] counter_1_q, counter_2_q, counter_3_q, counter_4_q, multiplexer_9_out, multiplexer_10_out;
  wire [31:0] register_1_q, register_2_q, register_3_q, register_4_q, register_9_q, register_10_q,
       register_11_q, register_12_q;

  or or_1 (write, w_b, w_j);
  Demultiplexer #(.select(2), .enable("false")) demultiplexer_1 (
    .out0(demultiplexer_1_out0), .out1(demultiplexer_1_out1), .out2(demultiplexer_1_out2),
    .out3(demultiplexer_1_out3), .in(write), .sel(multiplexer_7_out));
  // Probe on multiplexer_7_out
  Register #(.width(32)) register_1 (
    .D(inAddr), .en(demultiplexer_1_out0), .Q({register_1_q[31:12], addr1, register_1_q[1:0]}), .clk(clk));  // open: clr
  Register #(.width(32)) register_2 (
    .D(inAddr), .en(demultiplexer_1_out1), .Q({register_2_q[31:12], addr2, register_2_q[1:0]}), .clk(clk));  // open: clr
  Register #(.width(32)) register_3 (
    .D(inAddr), .en(demultiplexer_1_out2), .Q({register_3_q[31:12], addr3, register_3_q[1:0]}), .clk(clk));  // open: clr
  Register #(.width(32)) register_4 (
    .D(inAddr), .en(demultiplexer_1_out3), .Q({register_4_q[31:12], addr4, register_4_q[1:0]}), .clk(clk));  // open: clr
  Comparator #(.width(10), .mode("unsigned")) comparator_1 (
    .a(searchAddr[11:2]), .b(addr1), .eq(comparator_1_eq));  // open: gt, lt
  Comparator #(.width(10), .mode("unsigned")) comparator_2 (
    .a(searchAddr[11:2]), .b(addr2), .eq(comparator_2_eq));  // open: gt, lt
  Comparator #(.width(10), .mode("unsigned")) comparator_3 (
    .a(searchAddr[11:2]), .b(addr3), .eq(comparator_3_eq));  // open: gt, lt
  Comparator #(.width(10), .mode("unsigned")) comparator_4 (
    .a(searchAddr[11:2]), .b(addr4), .eq(comparator_4_eq));  // open: gt, lt
  Comparator #(.width(10), .mode("unsigned")) comparator_5 (
    .a(inAddr[11:2]), .b(addr1), .eq(comparator_5_eq));  // open: gt, lt
  Comparator #(.width(10), .mode("unsigned")) comparator_6 (
    .a(inAddr[11:2]), .b(addr2), .eq(comparator_6_eq));  // open: gt, lt
  Comparator #(.width(10), .mode("unsigned")) comparator_7 (
    .a(inAddr[11:2]), .b(addr3), .eq(comparator_7_eq));  // open: gt, lt
  Comparator #(.width(10), .mode("unsigned")) comparator_8 (
    .a(inAddr[11:2]), .b(addr4), .eq(comparator_8_eq));  // open: gt, lt
  and and_1 (and_1_out, comparator_1_eq, valid1);
  and and_2 (and_2_out, comparator_2_eq, valid2);
  and and_3 (and_3_out, comparator_3_eq, valid3);
  and and_4 (and_4_out, comparator_4_eq, valid4);
  or or_2 (hit, and_1_out, and_2_out, and_3_out, and_4_out);
  Register #(.width(1)) register_5 (
    .D(demultiplexer_1_out0), .en(demultiplexer_1_out0), .Q(valid1), .clk(clk));  // open: clr
  Register #(.width(1)) register_6 (
    .D(demultiplexer_1_out1), .en(demultiplexer_1_out1), .Q(valid2), .clk(clk));  // open: clr
  Register #(.width(1)) register_7 (
    .D(demultiplexer_1_out2), .en(demultiplexer_1_out2), .Q(valid3), .clk(clk));  // open: clr
  Register #(.width(1)) register_8 (
    .D(demultiplexer_1_out3), .en(demultiplexer_1_out3), .Q(valid4), .clk(clk));  // open: clr
  Priority_Encoder #(.select(2)) priority_encoder_1 (
    .in0(and_1_out), .in1(and_2_out), .in2(and_3_out), .in3(and_4_out), .out(Sel));  // open: gs, en_out, en_in
  and and_5 (and_5_out, comparator_5_eq, valid1);
  and and_6 (and_6_out, comparator_6_eq, valid2);
  and and_7 (and_7_out, comparator_7_eq, valid3);
  and and_8 (and_8_out, comparator_8_eq, valid4);
  Priority_Encoder #(.select(2)) priority_encoder_2 (
    .in0(and_5_out), .in1(and_6_out), .in2(and_7_out), .in3(and_8_out), .out(priority_encoder_2_out),
    .gs(priority_encoder_2_gs), .en_out(newRecord));  // open: en_in
  Register #(.width(32)) register_9 (
    .D(nextAddr), .en(demultiplexer_1_out0), .Q(register_9_q), .clk(clk));  // open: clr
  Register #(.width(32)) register_10 (
    .D(nextAddr), .en(demultiplexer_1_out1), .Q(register_10_q), .clk(clk));  // open: clr
  Register #(.width(32)) register_11 (
    .D(nextAddr), .en(demultiplexer_1_out2), .Q(register_11_q), .clk(clk));  // open: clr
  Register #(.width(32)) register_12 (
    .D(nextAddr), .en(demultiplexer_1_out3), .Q(register_12_q), .clk(clk));  // open: clr
  not not_1 (not_1_out, valid4);
  not not_2 (not_2_out, valid3);
  not not_3 (not_3_out, valid2);
  not not_4 (not_4_out, valid1);
  Pull_Resistor pull_resistor_1 (.node(targetAddr));
  Multiplexer #(.select(2), .width(32), .enable("false")) multiplexer_1 (
    .in0(register_9_q), .in1(register_10_q), .in2(register_11_q), .in3(register_12_q), .out(targetAddr),
    .sel(Sel));
  // Probe on Sel
  assign not_5_out = ~priority_encoder_3_out;  // NOT_Gate not_5, 2 bits wide
  Priority_Encoder #(.select(2)) priority_encoder_3 (
    .in0(not_1_out), .in1(not_2_out), .in2(not_3_out), .in3(not_4_out), .out(priority_encoder_3_out),
    .en_out(priority_encoder_3_en_out));  // open: gs, en_in
  Multiplexer #(.width(2), .enable("false")) multiplexer_2 (
    .in0(\预测状态跳转_1_nextstate ), .in1(2'b11), .out(multiplexer_2_out), .sel(newRecord));
  Multiplexer #(.width(2), .enable("false")) multiplexer_3 (
    .in0(\预测状态跳转_2_nextstate ), .in1(2'b11), .out(multiplexer_3_out), .sel(newRecord));
  Multiplexer #(.width(2), .enable("false")) multiplexer_4 (
    .in0(\预测状态跳转_3_nextstate ), .in1(2'b11), .out(multiplexer_4_out), .sel(newRecord));
  Multiplexer #(.width(2), .enable("false")) multiplexer_5 (
    .in0(\预测状态跳转_4_nextstate ), .in1(2'b11), .out(multiplexer_5_out), .sel(newRecord));
  Multiplexer #(.width(2), .enable("false")) multiplexer_6 (
    .in0(not_5_out), .in1(priority_encoder_4_out), .out(multiplexer_6_out), .sel(priority_encoder_3_en_out));
  \预测状态跳转  \u_预测状态跳转_1  (.Suc(success), .preState(register_13_q), .nextState(\预测状态跳转_1_nextstate ));
  Register #(.width(2)) register_13 (
    .D(multiplexer_2_out), .en(demultiplexer_1_out0), .Q(register_13_q), .clk(clk));  // open: clr
  \预测状态跳转  \u_预测状态跳转_2  (.Suc(success), .preState(register_14_q), .nextState(\预测状态跳转_2_nextstate ));
  Register #(.width(2)) register_14 (
    .D(multiplexer_3_out), .en(demultiplexer_1_out1), .Q(register_14_q), .clk(clk));  // open: clr
  \预测状态跳转  \u_预测状态跳转_3  (.Suc(success), .preState(register_15_q), .nextState(\预测状态跳转_3_nextstate ));
  Register #(.width(2)) register_15 (
    .D(multiplexer_4_out), .en(demultiplexer_1_out2), .Q(register_15_q), .clk(clk));  // open: clr
  \预测状态跳转  \u_预测状态跳转_4  (.Suc(success), .preState(register_16_q), .nextState(\预测状态跳转_4_nextstate ));
  Register #(.width(2)) register_16 (
    .D(multiplexer_5_out), .en(demultiplexer_1_out3), .Q(register_16_q), .clk(clk));  // open: clr
  Multiplexer #(.width(2), .enable("false")) multiplexer_7 (
    .in0(multiplexer_6_out), .in1(priority_encoder_2_out), .out(multiplexer_7_out),
    .sel(priority_encoder_2_gs));
  Pull_Resistor pull_resistor_2 (.node(nextState));
  Multiplexer #(.select(2), .width(2), .enable("false")) multiplexer_8 (
    .in0(register_13_q), .in1(register_14_q), .in2(register_15_q), .in3(register_16_q), .out(nextState),
    .sel(Sel));
  not not_6 (not_6_out, write);
  Counter #(.width(16), .max('hffff)) counter_1 (
    .load(demultiplexer_1_out0), .D({16{1'b0}}), .count(not_6_out), .Q(counter_1_q), .clk(clk));  // open: carry, clr
  Counter #(.width(16), .max('hffff)) counter_2 (
    .load(demultiplexer_1_out1), .D({16{1'b0}}), .count(not_6_out), .Q(counter_2_q), .clk(clk));  // open: carry, clr
  Counter #(.width(16), .max('hffff)) counter_3 (
    .load(demultiplexer_1_out2), .D({16{1'b0}}), .count(not_6_out), .Q(counter_3_q), .clk(clk));  // open: carry, clr
  Counter #(.width(16), .max('hffff)) counter_4 (
    .load(demultiplexer_1_out3), .D({16{1'b0}}), .count(not_6_out), .Q(counter_4_q), .clk(clk));  // open: carry, clr
  Comparator #(.width(16), .mode("unsigned")) comparator_9 (
    .a(counter_1_q), .b(counter_2_q), .lt(comparator_9_lt));  // open: gt, eq
  Multiplexer #(.width(16), .enable("false")) multiplexer_9 (
    .in0(counter_1_q), .in1(counter_2_q), .out(multiplexer_9_out), .sel(comparator_9_lt));
  Comparator #(.width(16), .mode("unsigned")) comparator_10 (
    .a(counter_3_q), .b(counter_4_q), .lt(comparator_10_lt));  // open: gt, eq
  Multiplexer #(.width(16), .enable("false")) multiplexer_10 (
    .in0(counter_3_q), .in1(counter_4_q), .out(multiplexer_10_out), .sel(comparator_10_lt));
  Comparator #(.width(16), .mode("unsigned")) comparator_11 (
    .a(multiplexer_9_out), .b(multiplexer_10_out), .lt(comparator_11_lt));  // open: gt, eq
  and and_9 (and_9_out, ~comparator_9_lt, ~comparator_11_lt);  // AND_Gate
  and and_10 (and_10_out, comparator_9_lt, ~comparator_11_lt);  // AND_Gate
  and and_11 (and_11_out, comparator_11_lt, ~comparator_10_lt);  // AND_Gate
  and and_12 (and_12_out, comparator_11_lt, comparator_10_lt);
  Priority_Encoder #(.select(2)) priority_encoder_4 (
    .in0(and_9_out), .in1(and_10_out), .in2(and_11_out), .in3(and_12_out), .out(priority_encoder_4_out));  // open: gs, en_out, en_in
endmodule
