// Logisim project ZY1501_U201514902_汤汇川_cpu_单级中断.circ as structural Verilog: 4 circuits, main circuit cpu
module cpu (
);

  wire ALUSrc, and_1_out, and_2_out, and_3_out, and_4_out, and_5_out, and_6_out, and_9_out, beq, bgez, bne,
       branchSuc, clk, cmp, comparator_1_gt, equal, Go, IR1, IR2, IR3, Jal, Jr, Jump, lh, MemRead, MemWrite,
       not_1_out, not_3_out, or_1_out, or_2_out, or_3_out, or_5_out, RegDst, register_1_q, RegWrite, RST,
       shift, syscall, W1, W2, W3, Zero_extend, \中断返回 , \停机 , \停机信号 , \数码管显示信号 , \暂停信号 ;
  wire [3:0] adder_1_out_2, control_1_aluop;
  wire [4:0] decoder_1_ra, decoder_1_rb, decoder_1_rw;
  wire [5:0] decoder_1_funct, decoder_1_opcode;
  wire [11:0] EX_PC, ID_PC, IF_PC, WB_PC;
  wire [15:0] \load_use次数 , \总周期数 , \插入气泡数 , \无条件分支指令数 , \有条件分支成功跳转 , \有条件分支指令数 ;
  wire [19:0] alu_1_p5_2;
  wire [27:0] adder_1_out, decoder_1_pc;
  wire [31:0] adder_2_out, alu_1_p5, dA, decoder_1_extend, mips_ram_1_p5, multiplexer_1_out,
       multiplexer_2_out, multiplexer_3_out, multiplexer_4_out, multiplexer_5_out, multiplexer_6_out,
       multiplexer_7_out, PC_q, registerfile_1_p8, rom_1_data, shifter_1_out, SyscallOut, \单级中断_1_pcout ;
  wire [31:16] multiplexer_7_out_2;

  Button \u_总复位  (.out(RST));
  Button _1 (.out(IR1));
  Button _2 (.out(IR2));
  Button _3 (.out(IR3));
  Button \u_继续运行  (.out(Go));
  LED led_1 (.in(W1));
  LED led_2 (.in(W2));
  LED led_3 (.in(W3));
  // Probe on IF_PC
  \单级中断  \u_单级中断_1  (
    .PC(PC_q), .nextPC(multiplexer_2_out), .clk(clk), .\_1号中断 (IR1), .\_1号中断等待指示灯 (W1), .\_2号中断 (IR2),
    .\_2号中断等待指示灯 (W2), .\_3号中断 (IR3), .\_3号中断等待指示灯 (W3), .\中断返回 (\中断返回 ), .PCout(\单级中断_1_pcout ));
  // Probe on \单级中断_1_pcout 
  not not_1 (not_1_out, or_1_out);
  or or_1 (or_1_out, \暂停信号 , \停机 );
  and and_1 (and_1_out, bne, ~equal);  // AND_Gate
  and and_2 (and_2_out, equal, beq);
  and and_3 (and_3_out, bgez, cmp);
  Hex_Digit_Display hex_digit_display_1 (.value(SyscallOut[31:28]));  // open: dp
  Register #(.width(32)) PC (.D(\单级中断_1_pcout ), .en(not_1_out), .Q(PC_q), .clk(clk), .clr(RST));
  or or_2 (or_2_out, Jal, Jump, Jr);
  and and_4 (and_4_out, or_2_out, ~\停机 );  // AND_Gate
  or or_3 (or_3_out, bne, beq, bgez);
  and and_5 (and_5_out, or_3_out, ~\停机 );  // AND_Gate
  and and_6 (and_6_out, ~\停机 , branchSuc);  // AND_Gate
  or or_4 (branchSuc, and_1_out, and_2_out, and_3_out);
  Hex_Digit_Display hex_digit_display_2 (.value(SyscallOut[23:20]));  // open: dp
  Hex_Digit_Display hex_digit_display_3 (.value(SyscallOut[27:24]));  // open: dp
  // Probe on ID_PC
  Adder #(.width(32)) adder_1 (.a(32'h4), .b(PC_q), .out({adder_1_out_2, adder_1_out}));  // open: cin, cout
  Counter #(.width(16), .max('hffff)) counter_1 (
    .count(and_4_out), .Q(\无条件分支指令数 ), .clk(clk), .clr(RST));  // open: load, D, carry
  Counter #(.width(16), .max('hffff)) counter_2 (
    .count(and_5_out), .Q(\有条件分支指令数 ), .clk(clk), .clr(RST));  // open: load, D, carry
  Counter #(.width(16), .max('hffff)) counter_3 (
    .count(and_6_out), .Q(\有条件分支成功跳转 ), .clk(clk), .clr(RST));  // open: load, D, carry
  Hex_Digit_Display hex_digit_display_4 (.value(SyscallOut[15:12]));  // open: dp
  Hex_Digit_Display hex_digit_display_5 (.value(SyscallOut[19:16]));  // open: dp
  ROM #(.addrWidth(10), .dataWidth(32)) rom_1 (.addr(PC_q[11:2]), .data(rom_1_data));  // open: sel
  Hex_Digit_Display hex_digit_display_6 (.value(SyscallOut[11:8]));  // open: dp
  Hex_Digit_Display hex_digit_display_7 (.value(SyscallOut[7:4]));  // open: dp
  // Probe on EX_PC
  Decoder decoder_1 (
    .CODE(rom_1_data), .PC(decoder_1_pc), .OPCODE(decoder_1_opcode), .FUNCT(decoder_1_funct),
    .RA(decoder_1_ra), .RB(decoder_1_rb), .RW(decoder_1_rw), .shift(shift), .RegDst(RegDst),
    .syscall(syscall), .Jal(Jal), .Zero_extend(Zero_extend), .extend(decoder_1_extend));
  Hex_Digit_Display hex_digit_display_8 (.value(SyscallOut[3:0]));  // open: dp
  // Probe on EX_PC
  Clock clock_1 (.out(clk));
  Multiplexer #(.width(32), .enable("false")) multiplexer_1 (
    .in0(multiplexer_6_out), .in1({adder_1_out_2, adder_1_out}), .out(multiplexer_1_out), .sel(Jal));
  // Probe on \总周期数 
  // Probe on \无条件分支指令数 
  // Probe on \有条件分支成功跳转 
  // Probe on \load_use次数 
  // Probe on \插入气泡数 
  // Probe on WB_PC
  Multiplexer #(.width(32), .enable("false")) multiplexer_2 (
    .in0(multiplexer_4_out), .in1(dA), .out(multiplexer_2_out), .sel(Jr));
  // Probe on decoder_1_rw
  // Probe on decoder_1_ra
  or or_5 (or_5_out, \停机信号 , \暂停信号 );
  // RegisterFile registerfile_1: pin names not known; wires that end beside it: multiplexer_1_out, clk, RegWrite, decoder_1_rw, decoder_1_ra, decoder_1_rb, dA, registerfile_1_p8
  // Probe on decoder_1_rb
  and and_7 (\停机 , or_5_out, syscall);
  Shifter #(.width(32)) shifter_1 (.in(decoder_1_extend), .\dist (5'b00010), .out(shifter_1_out));
  not not_2 (cmp, comparator_1_gt);
  Comparator #(.width(32)) comparator_1 (.a({32{1'b0}}), .b(dA), .gt(comparator_1_gt));  // open: eq, lt
  Multiplexer #(.width(32), .enable("false")) multiplexer_3 (
    .in0(registerfile_1_p8), .in1(decoder_1_extend), .out(multiplexer_3_out), .sel(ALUSrc));
  Control control_1 (
    .ALUOP(control_1_aluop), .shift(shift), .Zero_extend(Zero_extend), .ALUSrc(ALUSrc), .RegDst(RegDst),
    .RegWrite(RegWrite), .Jump(Jump), .beq(beq), .bne(bne), .MemRead(MemRead), .MemWrite(MemWrite),
    .Jal(Jal), .jr(Jr), .syscall(syscall), .bgez(bgez), .OPCODE(decoder_1_opcode), .FUNCT(decoder_1_funct),
    .lh(lh), .\中断返回 (\中断返回 ));
  Comparator #(.width(32), .mode("unsigned")) comparator_2 (.a(dA), .b(32'ha), .eq(\停机信号 ));  // open: gt, lt
  Comparator #(.width(32), .mode("unsigned")) comparator_3 (.a(dA), .b(32'h22), .eq(\数码管显示信号 ));  // open: gt, lt
  Register #(.width(1)) register_1 (.D(\停机 ), .Q(register_1_q), .clk(clk), .clr(RST));  // open: en
  not not_3 (not_3_out, register_1_q);
  Multiplexer #(.width(32), .enable("false")) multiplexer_4 (
    .in0(multiplexer_5_out), .in1({adder_1_out_2, decoder_1_pc}), .out(multiplexer_4_out), .sel(Jump));
  Multiplexer #(.width(32), .enable("false")) multiplexer_5 (
    .in0({adder_1_out_2, adder_1_out}), .in1(adder_2_out), .out(multiplexer_5_out), .sel(branchSuc));
  Adder #(.width(32)) adder_2 (
    .a({adder_1_out_2, adder_1_out}), .b(shifter_1_out), .out(adder_2_out));  // open: cin, cout
  // ALU alu_1: pin names not known; wires that end beside it: dA, multiplexer_3_out, control_1_aluop, equal, {alu_1_p5[31:22], alu_1_p5_2, alu_1_p5[1:0]}, {alu_1_p5[31:22], alu_1_p5_2, alu_1_p5[1:0]}, alu_1_p5_2, registerfile_1_p8
  and and_8 (\暂停信号 , ~\数码管显示信号 , ~\停机信号 , ~Go, syscall);  // AND_Gate
  Counter #(.width(16), .max('hffff)) counter_4 (
    .count(not_3_out), .Q(\总周期数 ), .clk(clk), .clr(RST));  // open: load, D, carry
  // Probe on {alu_1_p5[31:22], alu_1_p5_2, alu_1_p5[1:0]}
  and and_9 (and_9_out, \数码管显示信号 , syscall);
  // MIPS_RAM mips_ram_1: pin names not known; wires that end beside it: MemWrite, clk, MemRead, RST, mips_ram_1_p5
  Multiplexer #(.width(32), .enable("false")) multiplexer_6 (
    .in0({multiplexer_7_out_2, multiplexer_7_out[15:0]}), .in1(multiplexer_7_out), .out(multiplexer_6_out),
    .sel(lh));
  Register #(.width(32)) register_2 (.D(registerfile_1_p8), .en(and_9_out), .Q(SyscallOut), .clk(clk), .clr(RST));
  Multiplexer #(.width(32), .enable("false")) multiplexer_7 (
    .in0({alu_1_p5[31:22], alu_1_p5_2, alu_1_p5[1:0]}), .in1(mips_ram_1_p5),
    .out({multiplexer_7_out_2, multiplexer_7_out[15:0]}), .sel(MemRead));
  Pull_Resistor pull_resistor_1 (.node(multiplexer_7_out[15]));
  Multiplexer #(.width(16), .enable("false")) multiplexer_8 (
    .in0({16{1'b0}}), .in1({16{1'b1}}), .out(multiplexer_7_out[31:16]), .sel(multiplexer_7_out[15]));

  // Notes on the sheet:
  //   中断源
  //   中断请求指示
  //   指令存储器
  //   contents of rom_1 (hex, n*v repeats v):
  //   20110200 20020022 112020 c 2231ffff 1620fffc 20020032 c 20080001 20110010 112020 20020022 c 200b0020
  //   2288823 112020 20020022 c 216bffff 1560fffa 20020032 c 2008ffff 20117777 112020 20020022 c 200b0010
  //   3a31ffff 112020 20020022 c 216bffff 1560fffa 20020032 c 20090000 200b0010 34118483 20120404 118c00
  //   129400 36318281 22520404 ad310000 2328820 21290004 216bffff 1560fffb 200b0020 20090000 85310000
  //   112020 20020022 c 21290002 216bffff 1560fff9 20020032 c 2011000f 112020 20020022 c 2231ffff 621fffb
  //   2002000a c 27bdffe4 afb60000 afb50004 afb40008 afb3000c afb00010 afa40014 afa20018 20160001 20140006
  //   20150001 168020 108100 2149825 132020 20020022 c 1600fffa 295a022 1680fff7 8fb60000 8fb50004
  //   8fb40008 8fb3000c 8fb00010 8fa40014 8fa20018 27bd001c 42000018 27bdffe4 afb60000 afb50004 afb40008
  //   afb3000c afb00010 afa40014 afa20018 20160002 20140006 20150001 168020 108100 2149825 132020 20020022
  //   c 1600fffa 295a022 1680fff7 8fb60000 8fb50004 8fb40008 8fb3000c 8fb00010 8fa40014 8fa20018 27bd001c
  //   42000018 27bdffe4 afb60000 afb50004 afb40008 afb3000c afb00010 afa40014 afa20018 20160003 20140006
  //   20150001 168020 108100 2149825 132020 20020022 c 1600fffa 295a022 1680fff7 8fb60000 8fb50004
  //   8fb40008 8fb3000c 8fb00010 8fa40014 8fa20018 27bd001c 42000018
  //   数码管输出
  //   寄存器文件
endmodule

module Control (
  input  [5:0] OPCODE,
  input  [5:0] FUNCT,
  output [3:0] ALUOP,
  output MemRead,
  output shift,
  output ALUSrc,
  output Zero_extend,
  output RegDst,
  output Jump,
  output RegWrite,
  output beq,
  output bne,
  output MemWrite,
  output \中断返回 ,
  output Jal,
  output jr,
  output syscall,
  output bgez,
  output lh
);

  wire add, addi, addiu, addu, \and , andi, comparator_1_eq, comparator_17_eq, comparator_18_eq,
       comparator_19_eq, comparator_20_eq, comparator_21_eq, comparator_22_eq, comparator_23_eq,
       comparator_24_eq, comparator_25_eq, comparator_26_eq, comparator_27_eq, comparator_28_eq,
       comparator_29_eq, comparator_30_eq, COP0, eret, j, lw, \nor , \or , or_1_out, or_2_out, or_3_out,
       or_4_out, or_10_out, ori, sll, slt, slti, sltu, sra, srl, sub, subu, xori;

  Comparator #(.width(6)) comparator_1 (.a(OPCODE), .b({6{1'b0}}), .eq(comparator_1_eq));  // open: gt, lt
  Comparator #(.width(6)) comparator_2 (.a(OPCODE), .b(6'b001000), .eq(addi));  // open: gt, lt
  Comparator #(.width(6)) comparator_3 (.a(OPCODE), .b(6'b001001), .eq(addiu));  // open: gt, lt
  Comparator #(.width(6)) comparator_4 (.a(OPCODE), .b(6'b001100), .eq(andi));  // open: gt, lt
  Comparator #(.width(6)) comparator_5 (.a(OPCODE), .b(6'b001101), .eq(ori));  // open: gt, lt
  Comparator #(.width(6)) comparator_6 (.a(OPCODE), .b(6'b100011), .eq(lw));  // open: gt, lt
  Comparator #(.width(6)) comparator_7 (.a(OPCODE), .b(6'b101011), .eq(MemWrite));  // open: gt, lt
  Comparator #(.width(6)) comparator_8 (.a(OPCODE), .b(6'b000100), .eq(beq));  // open: gt, lt
  Comparator #(.width(6)) comparator_9 (.a(OPCODE), .b(6'b000101), .eq(bne));  // open: gt, lt
  Comparator #(.width(6)) comparator_10 (.a(OPCODE), .b(6'b001010), .eq(slti));  // open: gt, lt
  Comparator #(.width(6)) comparator_11 (.a(OPCODE), .b(6'b000010), .eq(j));  // open: gt, lt
  Comparator #(.width(6)) comparator_12 (.a(OPCODE), .b(6'b000011), .eq(Jal));  // open: gt, lt
  Comparator #(.width(6)) comparator_13 (.a(OPCODE), .b(6'b001110), .eq(xori));  // open: gt, lt
  Comparator #(.width(6)) comparator_14 (.a(OPCODE), .b(6'b100001), .eq(lh));  // open: gt, lt
  Comparator #(.width(6)) comparator_15 (.a(OPCODE), .b(6'b000001), .eq(bgez));  // open: gt, lt
  Comparator #(.width(6)) comparator_16 (.a(OPCODE), .b(6'b010000), .eq(COP0));  // open: gt, lt
  Comparator #(.width(6)) comparator_17 (.a(FUNCT), .b(6'b100000), .eq(comparator_17_eq));  // open: gt, lt
  Comparator #(.width(6)) comparator_18 (.a(FUNCT), .b(6'b100001), .eq(comparator_18_eq));  // open: gt, lt
  Comparator #(.width(6)) comparator_19 (.a(FUNCT), .b(6'b100100), .eq(comparator_19_eq));  // open: gt, lt
  Comparator #(.width(6)) comparator_20 (.a(FUNCT), .b({6{1'b0}}), .eq(comparator_20_eq));  // open: gt, lt
  Comparator #(.width(6)) comparator_21 (.a(FUNCT), .b(6'b000011), .eq(comparator_21_eq));  // open: gt, lt
  Comparator #(.width(6)) comparator_22 (.a(FUNCT), .b(6'b000010), .eq(comparator_22_eq));  // open: gt, lt
  Comparator #(.width(6)) comparator_23 (.a(FUNCT), .b(6'b100010), .eq(comparator_23_eq));  // open: gt, lt
  Comparator #(.width(6)) comparator_24 (.a(FUNCT), .b(6'b100101), .eq(comparator_24_eq));  // open: gt, lt
  Comparator #(.width(6)) comparator_25 (.a(FUNCT), .b(6'b100111), .eq(comparator_25_eq));  // open: gt, lt
  Comparator #(.width(6)) comparator_26 (.a(FUNCT), .b(6'b101010), .eq(comparator_26_eq));  // open: gt, lt
  Comparator #(.width(6)) comparator_27 (.a(FUNCT), .b(6'b101011), .eq(comparator_27_eq));  // open: gt, lt
  Comparator #(.width(6)) comparator_28 (.a(FUNCT), .b(6'b001000), .eq(comparator_28_eq));  // open: gt, lt
  Comparator #(.width(6)) comparator_29 (.a(FUNCT), .b(6'b001100), .eq(comparator_29_eq));  // open: gt, lt
  Comparator #(.width(6)) comparator_30 (.a(FUNCT), .b(6'b100011), .eq(comparator_30_eq));  // open: gt, lt
  Comparator #(.width(6)) comparator_31 (.a(FUNCT), .b(6'b011000), .eq(eret));  // open: gt, lt
  and and_1 (add, comparator_1_eq, comparator_17_eq);
  and and_2 (addu, comparator_1_eq, comparator_18_eq);
  and and_3 (\and , comparator_1_eq, comparator_19_eq);
  and and_4 (sll, comparator_1_eq, comparator_20_eq);
  and and_5 (sra, comparator_1_eq, comparator_21_eq);
  and and_6 (srl, comparator_1_eq, comparator_22_eq);
  and and_7 (sub, comparator_1_eq, comparator_23_eq);
  and and_8 (\or , comparator_1_eq, comparator_24_eq);
  and and_9 (\nor , comparator_1_eq, comparator_25_eq);
  and and_10 (slt, comparator_1_eq, comparator_26_eq);
  and and_11 (sltu, comparator_1_eq, comparator_27_eq);
  and and_12 (jr, comparator_1_eq, comparator_28_eq);
  and and_13 (syscall, comparator_1_eq, comparator_29_eq);
  and and_14 (subu, comparator_1_eq, comparator_30_eq);
  or or_1 (or_1_out, sub, subu);
  or or_2 (or_2_out, \and , andi);
  or or_3 (or_3_out, \or , ori);
  or or_4 (or_4_out, slt, slti);
  or or_5 (MemRead, lw, lh);
  or or_6 (shift, sll, sra, srl);
  or or_7 (Zero_extend, xori, andi, ori);
  or or_8 (RegDst, add, \nor , addu, \and , sll, sra, srl, \or , slt, sltu, subu, sub);
  or or_9 (Jump, j, Jal);
  or or_10 (or_10_out, add, addi, addiu, addu, lw, MemWrite, beq, bne, bgez, lh);
  Priority_Encoder #(.select(4)) priority_encoder_1 (
    .in0(sll), .in1(sra), .in2(srl), .in3(1'b0), .in4(1'b0), .in5(or_10_out), .in6(or_1_out), .in7(or_2_out),
    .in8(or_3_out), .in9(xori), .in10(\nor ), .in11(or_4_out), .in12(sltu), .in13(1'b0), .in14(1'b0),
    .in15(1'b0), .out(ALUOP));  // open: gs, en_out, en_in
  or or_11 (ALUSrc, addi, addiu, andi, sll, sra, srl, ori, lw, MemWrite, slti, xori, lh);
  or or_12 (RegWrite, slt, add, addiu, addu, \and , sll, sra, \nor , srl, \or , lh, sltu, subu, sub, addi, andi, ori, lw, slti, xori, Jal);
  and and_15 (\中断返回 , COP0, eret);

  // Other names for the same wires on the sheet: sw = MemWrite
endmodule

module Decoder (
  input  [31:0] CODE,
  input  shift,
  input  syscall,
  input  RegDst,
  input  Jal,
  input  Zero_extend,
  output [27:0] PC,
  output [5:0] OPCODE,
  output [5:0] FUNCT,
  output [4:0] RA,
  output [4:0] RB,
  output [4:0] RW,
  output [31:0] extend
);

  wire [4:0] multiplexer_1_out, multiplexer_2_out;
  wire [31:0] bit_extender_1_out, bit_extender_2_out, bit_extender_3_out, multiplexer_6_out;

  Shifter #(.width(28)) shifter_1 (.in(CODE[27:0]), .\dist (5'b00010), .out(PC));
  Multiplexer #(.width(5), .enable("false")) multiplexer_1 (
    .in0(CODE[25:21]), .in1(CODE[20:16]), .out(multiplexer_1_out), .sel(shift));
  Multiplexer #(.width(5), .enable("false")) multiplexer_2 (
    .in0(CODE[20:16]), .in1(CODE[15:11]), .out(multiplexer_2_out), .sel(RegDst));
  Multiplexer #(.width(5), .enable("false")) multiplexer_3 (
    .in0(multiplexer_1_out), .in1(5'b00010), .out(RA), .sel(syscall));
  Multiplexer #(.width(5), .enable("false")) multiplexer_4 (
    .in0(multiplexer_2_out), .in1({5{1'b1}}), .out(RW), .sel(Jal));
  assign bit_extender_1_out = {{16{CODE[15]}}, CODE[15:0]};  // Bit_Extender bit_extender_1
  assign bit_extender_2_out = {{16{1'b0}}, CODE[15:0]};  // Bit_Extender bit_extender_2
  assign bit_extender_3_out = {{27{1'b0}}, CODE[10:6]};  // Bit_Extender bit_extender_3
  Multiplexer #(.width(5), .enable("false")) multiplexer_5 (.in0(CODE[20:16]), .in1(5'b00100), .out(RB), .sel(syscall));
  Multiplexer #(.width(32), .enable("false")) multiplexer_6 (
    .in0(bit_extender_1_out), .in1(bit_extender_2_out), .out(multiplexer_6_out), .sel(Zero_extend));
  Multiplexer #(.width(32), .enable("false")) multiplexer_7 (
    .in0(multiplexer_6_out), .in1(bit_extender_3_out), .out(extend), .sel(shift));

  assign FUNCT = CODE[5:0];
  assign OPCODE = CODE[31:26];
endmodule

module \单级中断  (
  input  [31:0] PC,
  input  [31:0] nextPC,
  input  clk,
  input  \_1号中断 ,
  input  \_2号中断 ,
  input  \_3号中断 ,
  input  \中断返回 ,
  output [31:0] PCout,
  output \_1号中断等待指示灯 ,
  output \_2号中断等待指示灯 ,
  output \_3号中断等待指示灯 
);

  wire and_1_out, and_2_out, and_3_out, and_4_out, d_ff_1_q, d_ff_2_q, d_ff_3_q, d_ff_4_q, d_ff_5_q,
       d_ff_6_q, d_ff_7_q, IE, multiplexer_1_out, nand_1_out, nand_2_out, nand_3_out, or_4_out, or_5_out,
       or_6_out, or_7_out, priority_encoder_1_gs, \开启中断 ;
  wire [1:0] \中断屏蔽 ;
  wire [31:0] multiplexer_2_out, multiplexer_3_out, register_1_q;

  or or_1 (\_1号中断等待指示灯 , d_ff_5_q, d_ff_1_q);
  or or_2 (\_2号中断等待指示灯 , d_ff_6_q, d_ff_2_q);
  or or_3 (\_3号中断等待指示灯 , d_ff_7_q, d_ff_3_q);
  D_Flip_Flop d_ff_1 (.clk(\_1号中断 ), .D(1'b1), .Q(d_ff_1_q), .reset(d_ff_5_q));  // open: Qn, preset, en
  D_Flip_Flop d_ff_2 (.clk(\_2号中断 ), .D(1'b1), .Q(d_ff_2_q), .reset(d_ff_6_q));  // open: Qn, preset, en
  D_Flip_Flop d_ff_3 (.clk(\_3号中断 ), .D(1'b1), .Q(d_ff_3_q), .reset(d_ff_7_q));  // open: Qn, preset, en
  or or_4 (or_4_out, d_ff_1_q, d_ff_5_q);
  or or_5 (or_5_out, d_ff_2_q, d_ff_6_q);
  or or_6 (or_6_out, d_ff_3_q, d_ff_7_q);
  and and_1 (and_1_out, ~\中断返回 , or_7_out);  // AND_Gate
  or or_7 (or_7_out, \开启中断 , d_ff_4_q);
  D_Flip_Flop d_ff_4 (.clk(clk), .D(and_1_out), .Q(d_ff_4_q), .Qn(IE));  // open: preset, en, reset
  nand nand_1 (nand_1_out, \中断返回 , \中断屏蔽 [0], ~\中断屏蔽 [1]);  // NAND_Gate
  nand nand_2 (nand_2_out, \中断返回 , ~\中断屏蔽 [0], \中断屏蔽 [1]);  // NAND_Gate
  nand nand_3 (nand_3_out, \中断返回 , \中断屏蔽 [0], \中断屏蔽 [1]);
  and and_2 (and_2_out, or_4_out, nand_1_out);
  and and_3 (and_3_out, or_5_out, nand_2_out);
  and and_4 (and_4_out, or_6_out, nand_3_out);
  D_Flip_Flop d_ff_5 (.clk(clk), .D(and_2_out), .Q(d_ff_5_q));  // open: Qn, preset, en, reset
  D_Flip_Flop d_ff_6 (.clk(clk), .D(and_3_out), .Q(d_ff_6_q));  // open: Qn, preset, en, reset
  D_Flip_Flop d_ff_7 (.clk(clk), .D(and_4_out), .Q(d_ff_7_q));  // open: Qn, preset, en, reset
  Priority_Encoder #(.select(2)) priority_encoder_1 (
    .in0(1'b1), .in1(d_ff_5_q), .in2(d_ff_6_q), .in3(d_ff_7_q), .out(\中断屏蔽 ), .gs(priority_encoder_1_gs));  // open: en_out, en_in
  // Probe on \中断屏蔽 
  Multiplexer #(.select(2), .enable("false")) multiplexer_1 (
    .in0(1'b0), .in1(priority_encoder_1_gs), .in2(priority_encoder_1_gs), .in3(priority_encoder_1_gs),
    .out(multiplexer_1_out), .sel(\中断屏蔽 ));
  Register #(.width(32)) register_1 (.D(PC), .en(\开启中断 ), .Q(register_1_q), .clk(clk));  // open: clr
  Multiplexer #(.select(2), .width(32), .enable("false")) multiplexer_2 (
    .in0(nextPC), .in1(32'h110), .in2(32'h184), .in3(32'h1f8), .out(multiplexer_2_out), .sel(\中断屏蔽 ));
  and and_5 (\开启中断 , multiplexer_1_out, IE);
  Multiplexer #(.width(32), .enable("false")) multiplexer_3 (
    .in0(nextPC), .in1(multiplexer_2_out), .out(multiplexer_3_out), .sel(\开启中断 ));
  Multiplexer #(.width(32), .enable("false")) multiplexer_4 (
    .in0(multiplexer_3_out), .in1(register_1_q), .out(PCout), .sel(\中断返回 ));
endmodule
