// Logisim project ZY1501_U201514902_汤汇川_cpu_流水.circ as structural Verilog: 7 circuits, main circuit cpu
module cpu (
);

  wire alu_1_p4, and_1_out, and_2_out, and_3_out, and_4_out, and_5_out, and_6_out, and_8_out, beq, bgez, bne,
       branch, branch_Suc, clk, cmp, comparator_2_gt, control_1_alusrc, control_1_lh, control_1_memread,
       control_1_memwrite, control_1_regdst, control_1_regwrite, control_1_shift, control_1_zero_extend,
       equal, ex_mem_1_lh_2, ex_mem_1_memread_2, ex_mem_1_memwrite_2, ex_mem_1_regwrite_2, ex_mem_1_stopout,
       id_ex_1_alusrcout, id_ex_1_lhout, id_ex_1_memreadout, id_ex_1_memwriteout, id_ex_1_regwrite_2,
       id_ex_1_stopout, id_ex_1_syscallout, Jal, Jr, Jump, lh, mem_wb_1_stopout, not_1_out, not_2_out,
       or_1_out, or_2_out, Pause, RegWrite, RST, stop, syscall;
  wire [3:0] control_1_aluop, id_ex_1_aluopout, if_id_1_npcout_2;
  wire [4:0] decoder_1_ra, decoder_1_rb, decoder_1_rw, ex_mem_1_rwout, id_ex_1_rwout, rW;
  wire [5:0] decoder_1_funct, decoder_1_opcode;
  wire [15:0] \总周期数 , \无条件分支指令数 , \有条件分支成功跳转 , \有条件分支指令数 ;
  wire [27:0] decoder_1_pc, if_id_1_npcout;
  wire [31:0] adder_1_out, adder_2_out, alu_1_p2, alu_1_p5, alu_1_p6, decoder_1_extend, ex_mem_1_npcout,
       ex_mem_1_rbout, id_ex_1_extendout, id_ex_1_npcout, id_ex_1_raout, id_ex_1_rbout, if_id_1_irout,
       mem_wb_1_drout, mips_ram_1_p7, multiplexer_1_out, multiplexer_2_out, multiplexer_3_out,
       multiplexer_4_out, multiplexer_6_out, multiplexer_7_out, NPC, PC_q, registerfile_1_p7,
       registerfile_1_p8, rom_1_data, shifter_1_out, SyscallOut, writeData;
  wire [31:16] multiplexer_9_out;

  Button \u_总复位  (.out(RST));
  not not_1 (not_1_out, Pause);
  Register #(.width(32)) PC (.D(multiplexer_1_out), .en(not_1_out), .Q(PC_q), .clk(clk), .clr(RST));
  and and_1 (and_1_out, bne, ~equal);  // AND_Gate
  and and_2 (and_2_out, equal, beq);
  and and_3 (and_3_out, bgez, cmp);
  Hex_Digit_Display hex_digit_display_1 (.value(SyscallOut[27:24]));  // open: dp
  Hex_Digit_Display hex_digit_display_2 (.value(SyscallOut[31:28]));  // open: dp
  Adder #(.width(32)) adder_1 (.a(32'h4), .b(PC_q), .out(adder_1_out));  // open: cin, cout
  or or_1 (or_1_out, Jal, Jump, Jr);
  and and_4 (and_4_out, or_1_out, ~stop);  // AND_Gate
  or or_2 (or_2_out, bne, beq, bgez);
  and and_5 (and_5_out, or_2_out, ~stop);  // AND_Gate
  and and_6 (and_6_out, ~stop, branch_Suc);  // AND_Gate
  or or_3 (branch_Suc, and_1_out, and_2_out, and_3_out);
  Hex_Digit_Display hex_digit_display_3 (.value(SyscallOut[19:16]));  // open: dp
  Hex_Digit_Display hex_digit_display_4 (.value(SyscallOut[23:20]));  // open: dp
  Multiplexer #(.width(32), .enable("false")) multiplexer_1 (
    .in0(adder_1_out), .in1(multiplexer_2_out), .out(multiplexer_1_out), .sel(branch));
  Counter #(.width(16), .max('hffff)) counter_1 (
    .count(and_4_out), .Q(\无条件分支指令数 ), .clk(clk), .clr(RST));  // open: load, D, carry
  Counter #(.width(16), .max('hffff)) counter_2 (
    .count(and_5_out), .Q(\有条件分支指令数 ), .clk(clk), .clr(RST));  // open: load, D, carry
  Counter #(.width(16), .max('hffff)) counter_3 (
    .count(and_6_out), .Q(\有条件分支成功跳转 ), .clk(clk), .clr(RST));  // open: load, D, carry
  Hex_Digit_Display hex_digit_display_5 (.value(SyscallOut[11:8]));  // open: dp
  Hex_Digit_Display hex_digit_display_6 (.value(SyscallOut[15:12]));  // open: dp
  IF_ID if_id_1 (
    .NPC(adder_1_out), .IR(rom_1_data), .NPCout({if_id_1_npcout_2, if_id_1_npcout}), .IRout(if_id_1_irout),
    .clk(clk), .RST(RST), .stop(Pause));
  ROM #(.addrWidth(10), .dataWidth(32)) rom_1 (.addr(PC_q[11:2]), .data(rom_1_data));  // open: sel
  Hex_Digit_Display hex_digit_display_7 (.value(SyscallOut[7:4]));  // open: dp
  Hex_Digit_Display hex_digit_display_8 (.value(SyscallOut[3:0]));  // open: dp
  Multiplexer #(.width(32), .enable("false")) multiplexer_2 (
    .in0(multiplexer_3_out), .in1(registerfile_1_p7), .out(multiplexer_2_out), .sel(Jr));
  Decoder decoder_1 (
    .CODE(if_id_1_irout), .PC(decoder_1_pc), .OPCODE(decoder_1_opcode), .FUNCT(decoder_1_funct),
    .RA(decoder_1_ra), .RB(decoder_1_rb), .RW(decoder_1_rw), .shift(control_1_shift),
    .RegDst(control_1_regdst), .syscall(syscall), .Jal(Jal), .Zero_extend(control_1_zero_extend),
    .extend(decoder_1_extend));
  Control control_1 (
    .ALUOP(control_1_aluop), .shift(control_1_shift), .Zero_extend(control_1_zero_extend),
    .ALUSrc(control_1_alusrc), .RegDst(control_1_regdst), .RegWrite(control_1_regwrite), .Jump(Jump),
    .beq(beq), .bne(bne), .MemRead(control_1_memread), .MemWrite(control_1_memwrite), .Jal(Jal), .jr(Jr),
    .syscall(syscall), .bgez(bgez), .OPCODE(decoder_1_opcode), .FUNCT(decoder_1_funct), .lh(control_1_lh));
  Clock clock_1 (.out(clk));
  Multiplexer #(.width(32), .enable("false")) multiplexer_3 (
    .in0(multiplexer_4_out), .in1({if_id_1_npcout_2, decoder_1_pc}), .out(multiplexer_3_out), .sel(Jump));
  or or_4 (branch, Jal, Jump, Jr, bne, beq, bgez);
  // Probe on \总周期数 
  // Probe on \无条件分支指令数 
  // Probe on \有条件分支指令数 
  // Probe on \有条件分支成功跳转 
  Multiplexer #(.width(32), .enable("false")) multiplexer_4 (
    .in0({if_id_1_npcout_2, if_id_1_npcout}), .in1(adder_2_out), .out(multiplexer_4_out), .sel(branch_Suc));
  // RegisterFile registerfile_1: pin names not known; wires that end beside it: writeData, clk, RegWrite, rW, decoder_1_ra, decoder_1_rb, registerfile_1_p7, registerfile_1_p8
  // Probe on decoder_1_rb
  Shifter #(.width(32)) shifter_1 (.in(decoder_1_extend), .\dist (5'b00010), .out(shifter_1_out));
  Comparator #(.width(32), .mode("unsigned")) comparator_1 (
    .a(registerfile_1_p7), .b(32'ha), .eq(equal));  // open: gt, lt
  not not_2 (not_2_out, stop);
  not not_3 (cmp, comparator_2_gt);
  Adder #(.width(32)) adder_2 (
    .a({if_id_1_npcout_2, if_id_1_npcout}), .b(shifter_1_out), .out(adder_2_out));  // open: cin, cout
  Comparator #(.width(32)) comparator_2 (.a({32{1'b0}}), .b(registerfile_1_p7), .gt(comparator_2_gt));  // open: eq, lt
  and and_7 (Pause, equal, syscall);
  Counter #(.width(16), .max('hffff)) counter_4 (
    .count(not_2_out), .Q(\总周期数 ), .clk(clk), .clr(RST));  // open: load, D, carry
  ID_EX id_ex_1 (
    .rA(registerfile_1_p7), .rB(registerfile_1_p8), .extend(decoder_1_extend), .ALUSrc(control_1_alusrc),
    .Syscall(syscall), .MemRead(control_1_memread), .MemWrite(control_1_memwrite),
    .RegWrite(control_1_regwrite), .NPC({if_id_1_npcout_2, if_id_1_npcout}), .RW(decoder_1_rw),
    .rAout(id_ex_1_raout), .rBout(id_ex_1_rbout), .extendout(id_ex_1_extendout),
    .ALUSrcout(id_ex_1_alusrcout), .Syscallout(id_ex_1_syscallout), .MemReadout(id_ex_1_memreadout),
    .MemWriteout(id_ex_1_memwriteout), .RegWrite_2(id_ex_1_regwrite_2), .NPCout(id_ex_1_npcout),
    .RWout(id_ex_1_rwout), .clk(clk), .RST(RST), .lh(control_1_lh), .lhout(id_ex_1_lhout),
    .ALUOP(control_1_aluop), .ALUOPout(id_ex_1_aluopout), .Stopout(id_ex_1_stopout), .stop(Pause),
    .stop_2(stop));
  // ALU alu_1: pin names not known; wires that end beside it: id_ex_1_raout, alu_1_p2, id_ex_1_aluopout, alu_1_p4, alu_1_p5, alu_1_p6
  Multiplexer #(.width(32), .enable("false")) multiplexer_5 (
    .in0(id_ex_1_rbout), .in1(id_ex_1_extendout), .out(alu_1_p2), .sel(id_ex_1_alusrcout));
  Register #(.width(32)) register_1 (.en(and_8_out), .Q(SyscallOut), .clk(clk), .clr(RST));  // open: D
  and and_8 (and_8_out, ~alu_1_p4, id_ex_1_syscallout);  // AND_Gate
  EX_MEM ex_mem_1 (
    .NPC(id_ex_1_npcout), .ALURes(alu_1_p5), .rB(id_ex_1_rbout), .MemWrite(id_ex_1_memwriteout),
    .MemRead(id_ex_1_memreadout), .lh(id_ex_1_lhout), .rW(id_ex_1_rwout), .NPCout(ex_mem_1_npcout),
    .ALUout(alu_1_p6), .rBout(ex_mem_1_rbout), .MemWrite_2(ex_mem_1_memwrite_2),
    .MemRead_2(ex_mem_1_memread_2), .lh_2(ex_mem_1_lh_2), .rWout(ex_mem_1_rwout), .clk(clk), .rst(RST),
    .RegWrite(id_ex_1_regwrite_2), .RegWrite_2(ex_mem_1_regwrite_2), .Stop(id_ex_1_stopout),
    .Stopout(ex_mem_1_stopout), .stop_2(stop));
  Multiplexer #(.width(32), .enable("false")) multiplexer_6 (
    .in0(alu_1_p6), .in1(mips_ram_1_p7), .out(multiplexer_6_out), .sel(ex_mem_1_memread_2));
  // MIPS_RAM mips_ram_1: pin names not known; wires that end beside it: alu_1_p6[21:2], ex_mem_1_rbout, ex_mem_1_memwrite_2, clk, ex_mem_1_memread_2, RST, mips_ram_1_p7
  MEM_WB mem_wb_1 (
    .NPC(ex_mem_1_npcout), .DR(multiplexer_6_out), .rW(ex_mem_1_rwout), .lh(ex_mem_1_lh_2),
    .RegWrite(ex_mem_1_regwrite_2), .Stopin(ex_mem_1_stopout), .NPCout(NPC), .DRout(mem_wb_1_drout),
    .rWout(rW), .lhout(lh), .RegWriteout(RegWrite), .Stopout(mem_wb_1_stopout), .clk(clk), .rst(RST),
    .stop(stop));
  Register #(.width(1)) register_2 (.D(mem_wb_1_stopout), .Q(stop), .clk(clk), .clr(RST));  // open: en
  Multiplexer #(.width(32), .enable("false")) multiplexer_7 (
    .in0(mem_wb_1_drout), .in1({multiplexer_9_out, mem_wb_1_drout[15:0]}), .out(multiplexer_7_out), .sel(lh));
  Multiplexer #(.width(32), .enable("false")) multiplexer_8 (
    .in0(multiplexer_7_out), .in1(NPC), .out(writeData), .sel(Jal));
  Pull_Resistor pull_resistor_1 (.node(mem_wb_1_drout[15]));
  Multiplexer #(.width(16), .enable("false")) multiplexer_9 (
    .in0({16{1'b0}}), .in1({16{1'b1}}), .out(multiplexer_9_out), .sel(mem_wb_1_drout[15]));

  // Notes on the sheet:
  //   总复位信号应将除ROM以外所有存储组件全部清零
  //   数码管输出应该用寄存器锁存，否则显示数据只能一闪而过
  //   可以通过项目增加Logisim库的方式将前几次实验完成的电路作为子电路引入到本电路中使用
  //   指令存储器
  //   contents of rom_1 (hex, n*v repeats v):
  //   20100000 20110000 20120000 20130000 36100000 36310001 36520002 36730003 ae100000 ae110004 ae120008
  //   ae13000c 2002000a 20110000 20120000 20130000 c
  //   数码管输出
  //   寄存器文件
endmodule

module Control (
  input  [5:0] OPCODE,
  input  [5:0] FUNCT,
  output [3:0] ALUOP,
  output MemRead,
  output shift,
  output ALUSrc,
  output Zero_extend,
  output RegDst,
  output Jump,
  output RegWrite,
  output beq,
  output bne,
  output MemWrite,
  output Jal,
  output jr,
  output syscall,
  output bgez,
  output lh
);

  wire add, addi, addiu, addu, \and , andi, comparator_1_eq, comparator_16_eq, comparator_17_eq,
       comparator_18_eq, comparator_19_eq, comparator_20_eq, comparator_21_eq, comparator_22_eq,
       comparator_23_eq, comparator_24_eq, comparator_25_eq, comparator_26_eq, comparator_27_eq,
       comparator_28_eq, comparator_29_eq, j, lw, \nor , \or , or_1_out, or_2_out, or_3_out, or_4_out,
       or_10_out, ori, sll, slt, slti, sltu, sra, srl, sub, subu, xori;

  Comparator #(.width(6)) comparator_1 (.a(OPCODE), .b({6{1'b0}}), .eq(comparator_1_eq));  // open: gt, lt
  Comparator #(.width(6)) comparator_2 (.a(OPCODE), .b(6'b001000), .eq(addi));  // open: gt, lt
  Comparator #(.width(6)) comparator_3 (.a(OPCODE), .b(6'b001001), .eq(addiu));  // open: gt, lt
  Comparator #(.width(6)) comparator_4 (.a(OPCODE), .b(6'b001100), .eq(andi));  // open: gt, lt
  Comparator #(.width(6)) comparator_5 (.a(OPCODE), .b(6'b001101), .eq(ori));  // open: gt, lt
  Comparator #(.width(6)) comparator_6 (.a(OPCODE), .b(6'b100011), .eq(lw));  // open: gt, lt
  Comparator #(.width(6)) comparator_7 (.a(OPCODE), .b(6'b101011), .eq(MemWrite));  // open: gt, lt
  Comparator #(.width(6)) comparator_8 (.a(OPCODE), .b(6'b000100), .eq(beq));  // open: gt, lt
  Comparator #(.width(6)) comparator_9 (.a(OPCODE), .b(6'b000101), .eq(bne));  // open: gt, lt
  Comparator #(.width(6)) comparator_10 (.a(OPCODE), .b(6'b001010), .eq(slti));  // open: gt, lt
  Comparator #(.width(6)) comparator_11 (.a(OPCODE), .b(6'b000010), .eq(j));  // open: gt, lt
  Comparator #(.width(6)) comparator_12 (.a(OPCODE), .b(6'b000011), .eq(Jal));  // open: gt, lt
  Comparator #(.width(6)) comparator_13 (.a(OPCODE), .b(6'b001110), .eq(xori));  // open: gt, lt
  Comparator #(.width(6)) comparator_14 (.a(OPCODE), .b(6'b100001), .eq(lh));  // open: gt, lt
  Comparator #(.width(6)) comparator_15 (.a(OPCODE), .b(6'b000001), .eq(bgez));  // open: gt, lt
  Comparator #(.width(6)) comparator_16 (.a(FUNCT), .b(6'b100000), .eq(comparator_16_eq));  // open: gt, lt
  Comparator #(.width(6)) comparator_17 (.a(FUNCT), .b(6'b100001), .eq(comparator_17_eq));  // open: gt, lt
  Comparator #(.width(6)) comparator_18 (.a(FUNCT), .b(6'b100100), .eq(comparator_18_eq));  // open: gt, lt
  Comparator #(.width(6)) comparator_19 (.a(FUNCT), .b({6{1'b0}}), .eq(comparator_19_eq));  // open: gt, lt
  Comparator #(.width(6)) comparator_20 (.a(FUNCT), .b(6'b000011), .eq(comparator_20_eq));  // open: gt, lt
  Comparator #(.width(6)) comparator_21 (.a(FUNCT), .b(6'b000010), .eq(comparator_21_eq));  // open: gt, lt
  Comparator #(.width(6)) comparator_22 (.a(FUNCT), .b(6'b100010), .eq(comparator_22_eq));  // open: gt, lt
  Comparator #(.width(6)) comparator_23 (.a(FUNCT), .b(6'b100101), .eq(comparator_23_eq));  // open: gt, lt
  Comparator #(.width(6)) comparator_24 (.a(FUNCT), .b(6'b100111), .eq(comparator_24_eq));  // open: gt, lt
  Comparator #(.width(6)) comparator_25 (.a(FUNCT), .b(6'b101010), .eq(comparator_25_eq));  // open: gt, lt
  Comparator #(.width(6)) comparator_26 (.a(FUNCT), .b(6'b101011), .eq(comparator_26_eq));  // open: gt, lt
  Comparator #(.width(6)) comparator_27 (.a(FUNCT), .b(6'b001000), .eq(comparator_27_eq));  // open: gt, lt
  Comparator #(.width(6)) comparator_28 (.a(FUNCT), .b(6'b001100), .eq(comparator_28_eq));  // open: gt, lt
  Comparator #(.width(6)) comparator_29 (.a(FUNCT), .b(6'b100011), .eq(comparator_29_eq));  // open: gt, lt
  and and_1 (add, comparator_1_eq, comparator_16_eq);
  and and_2 (addu, comparator_1_eq, comparator_17_eq);
  and and_3 (\and , comparator_1_eq, comparator_18_eq);
  and and_4 (sll, comparator_1_eq, comparator_19_eq);
  and and_5 (sra, comparator_1_eq, comparator_20_eq);
  and and_6 (srl, comparator_1_eq, comparator_21_eq);
  and and_7 (sub, comparator_1_eq, comparator_22_eq);
  and and_8 (\or , comparator_1_eq, comparator_23_eq);
  and and_9 (\nor , comparator_1_eq, comparator_24_eq);
  and and_10 (slt, comparator_1_eq, comparator_25_eq);
  and and_11 (sltu, comparator_1_eq, comparator_26_eq);
  and and_12 (jr, comparator_1_eq, comparator_27_eq);
  and and_13 (syscall, comparator_1_eq, comparator_28_eq);
  and and_14 (subu, comparator_1_eq, comparator_29_eq);
  or or_1 (or_1_out, sub, subu);
  or or_2 (or_2_out, \and , andi);
  or or_3 (or_3_out, \or , ori);
  or or_4 (or_4_out, slt, slti);
  or or_5 (MemRead, lw, lh);
  or or_6 (shift, sll, sra, srl);
  or or_7 (Zero_extend, xori, andi, ori);
  or or_8 (RegDst, add, \nor , addu, \and , sll, sra, srl, \or , slt, sltu, subu, sub);
  or or_9 (Jump, j, Jal);
  or or_10 (or_10_out, add, addi, addiu, addu, lw, MemWrite, beq, bne, bgez, lh);
  Priority_Encoder #(.select(4)) priority_encoder_1 (
    .in0(sll), .in1(sra), .in2(srl), .in3(1'b0), .in4(1'b0), .in5(or_10_out), .in6(or_1_out), .in7(or_2_out),
    .in8(or_3_out), .in9(xori), .in10(\nor ), .in11(or_4_out), .in12(sltu), .in13(1'b0), .in14(1'b0),
    .in15(1'b0), .out(ALUOP));  // open: gs, en_out, en_in
  or or_11 (ALUSrc, addi, addiu, andi, sll, sra, srl, ori, lw, MemWrite, slti, xori, lh);
  or or_12 (RegWrite, slt, add, addiu, addu, \and , sll, sra, \nor , srl, \or , lh, sltu, subu, sub, addi, andi, ori, lw, slti, xori, Jal);

  // Other names for the same wires on the sheet: sw = MemWrite
endmodule

module Decoder (
  input  [31:0] CODE,
  input  shift,
  input  syscall,
  input  RegDst,
  input  Jal,
  input  Zero_extend,
  output [27:0] PC,
  output [5:0] OPCODE,
  output [5:0] FUNCT,
  output [4:0] RA,
  output [4:0] RB,
  output [4:0] RW,
  output [31:0] extend
);

  wire [4:0] multiplexer_1_out, multiplexer_2_out;
  wire [31:0] bit_extender_1_out, bit_extender_2_out, bit_extender_3_out, multiplexer_6_out;

  Shifter #(.width(28)) shifter_1 (.in(CODE[27:0]), .\dist (5'b00010), .out(PC));
  Multiplexer #(.width(5), .enable("false")) multiplexer_1 (
    .in0(CODE[25:21]), .in1(CODE[20:16]), .out(multiplexer_1_out), .sel(shift));
  Multiplexer #(.width(5), .enable("false")) multiplexer_2 (
    .in0(CODE[20:16]), .in1(CODE[15:11]), .out(multiplexer_2_out), .sel(RegDst));
  // Probe on CODE[15:0]
  Multiplexer #(.width(5), .enable("false")) multiplexer_3 (
    .in0(multiplexer_1_out), .in1(5'b00010), .out(RA), .sel(syscall));
  Multiplexer #(.width(5), .enable("false")) multiplexer_4 (
    .in0(multiplexer_2_out), .in1({5{1'b1}}), .out(RW), .sel(Jal));
  assign bit_extender_1_out = {{16{CODE[15]}}, CODE[15:0]};  // Bit_Extender bit_extender_1
  assign bit_extender_2_out = {{16{1'b0}}, CODE[15:0]};  // Bit_Extender bit_extender_2
  assign bit_extender_3_out = {{27{1'b0}}, CODE[10:6]};  // Bit_Extender bit_extender_3
  Multiplexer #(.width(5), .enable("false")) multiplexer_5 (.in0(CODE[20:16]), .in1(5'b00100), .out(RB), .sel(syscall));
  Multiplexer #(.width(32), .enable("false")) multiplexer_6 (
    .in0(bit_extender_1_out), .in1(bit_extender_2_out), .out(multiplexer_6_out), .sel(Zero_extend));
  // Probe on bit_extender_3_out
  Multiplexer #(.width(32), .enable("false")) multiplexer_7 (
    .in0(multiplexer_6_out), .in1(bit_extender_3_out), .out(extend), .sel(shift));

  assign FUNCT = CODE[5:0];
  assign OPCODE = CODE[31:26];
endmodule

module IF_ID (
  input  [31:0] NPC,
  input  [31:0] IR,
  input  clk,
  input  RST,
  input  stop,
  output [31:0] NPCout,
  output [31:0] IRout
);

  wire not_1_out;

  not not_1 (not_1_out, stop);
  Register #(.width(32)) u_NPC (.D(NPC), .en(not_1_out), .Q(NPCout), .clk(clk), .clr(RST));
  Register #(.width(32)) u_IR (.D(IR), .en(not_1_out), .Q(IRout), .clk(clk), .clr(RST));
endmodule

module ID_EX (
  input  [31:0] rA,
  input  [31:0] rB,
  input  [31:0] extend,
  input  ALUSrc,
  input  Syscall,
  input  MemRead,
  input  MemWrite,
  input  RegWrite,
  input  lh,
  input  [3:0] ALUOP,
  input  [31:0] NPC,
  input  [4:0] RW,
  input  stop,
  input  clk,
  input  RST,
  input  stop_2,
  output [31:0] rAout,
  output [31:0] rBout,
  output [31:0] extendout,
  output ALUSrcout,
  output Syscallout,
  output MemReadout,
  output MemWriteout,
  output RegWrite_2,
  output lhout,
  output [3:0] ALUOPout,
  output [31:0] NPCout,
  output [4:0] RWout,
  output Stopout
);

  wire not_1_out;

  Register #(.width(32)) register_1 (.D(rA), .en(not_1_out), .Q(rAout), .clk(clk), .clr(RST));
  Register #(.width(32)) register_2 (.D(rB), .en(not_1_out), .Q(rBout), .clk(clk), .clr(RST));
  Register #(.width(32)) register_3 (.D(extend), .en(not_1_out), .Q(extendout), .clk(clk), .clr(RST));
  Register #(.width(1)) register_4 (.D(ALUSrc), .en(not_1_out), .Q(ALUSrcout), .clk(clk), .clr(RST));
  Register #(.width(1)) register_5 (.D(Syscall), .en(not_1_out), .Q(Syscallout), .clk(clk), .clr(RST));
  Register #(.width(1)) register_6 (.D(MemRead), .en(not_1_out), .Q(MemReadout), .clk(clk), .clr(RST));
  Register #(.width(1)) register_7 (.D(MemWrite), .en(not_1_out), .Q(MemWriteout), .clk(clk), .clr(RST));
  Register #(.width(1)) register_8 (.D(RegWrite), .en(not_1_out), .Q(RegWrite_2), .clk(clk), .clr(RST));
  Register #(.width(1)) register_9 (.D(lh), .en(not_1_out), .Q(lhout), .clk(clk), .clr(RST));
  Register #(.width(4)) register_10 (.D(ALUOP), .en(not_1_out), .Q(ALUOPout), .clk(clk), .clr(RST));
  Register #(.width(32)) register_11 (.D(NPC), .en(not_1_out), .Q(NPCout), .clk(clk), .clr(RST));
  Register #(.width(5)) register_12 (.D(RW), .en(not_1_out), .Q(RWout), .clk(clk), .clr(RST));
  Register #(.width(1)) register_13 (.D(stop), .en(not_1_out), .Q(Stopout), .clk(clk), .clr(RST));
  not not_1 (not_1_out, stop_2);
endmodule

module EX_MEM (
  input  [31:0] NPC,
  input  [31:0] ALURes,
  input  [31:0] rB,
  input  MemWrite,
  input  MemRead,
  input  lh,
  input  [4:0] rW,
  input  RegWrite,
  input  Stop,
  input  clk,
  input  rst,
  input  stop_2,
  output [31:0] NPCout,
  output [31:0] ALUout,
  output [31:0] rBout,
  output MemWrite_2,
  output MemRead_2,
  output lh_2,
  output [4:0] rWout,
  output RegWrite_2,
  output Stopout
);

  wire not_1_out;

  not not_1 (not_1_out, stop_2);
  Register #(.width(32)) register_1 (.D(NPC), .en(not_1_out), .Q(NPCout), .clk(clk), .clr(rst));
  Register #(.width(32)) register_2 (.D(ALURes), .en(not_1_out), .Q(ALUout), .clk(clk), .clr(rst));
  Register #(.width(32)) register_3 (.D(rB), .en(not_1_out), .Q(rBout), .clk(clk), .clr(rst));
  Register #(.width(1)) register_4 (.D(MemWrite), .en(not_1_out), .Q(MemWrite_2), .clk(clk), .clr(rst));
  Register #(.width(1)) register_5 (.D(MemRead), .en(not_1_out), .Q(MemRead_2), .clk(clk), .clr(rst));
  Register #(.width(1)) register_6 (.D(lh), .en(not_1_out), .Q(lh_2), .clk(clk), .clr(rst));
  Register #(.width(5)) register_7 (.D(rW), .en(not_1_out), .Q(rWout), .clk(clk), .clr(rst));
  Register #(.width(1)) register_8 (.D(RegWrite), .en(not_1_out), .Q(RegWrite_2), .clk(clk), .clr(rst));
  Register #(.width(1)) register_9 (.D(Stop), .en(not_1_out), .Q(Stopout), .clk(clk), .clr(rst));
endmodule

module MEM_WB (
  input  [31:0] NPC,
  input  [31:0] DR,
  input  [4:0] rW,
  input  lh,
  input  RegWrite,
  input  Stopin,
  input  clk,
  input  rst,
  input  stop,
  output [31:0] NPCout,
  output [31:0] DRout,
  output [4:0] rWout,
  output lhout,
  output RegWriteout,
  output Stopout
);

  wire not_1_out;

  not not_1 (not_1_out, stop);
  Register #(.width(32)) register_1 (.D(NPC), .en(not_1_out), .Q(NPCout), .clk(clk), .clr(rst));
  Register #(.width(32)) register_2 (.D(DR), .en(not_1_out), .Q(DRout), .clk(clk), .clr(rst));
  Register #(.width(5)) register_3 (.D(rW), .en(not_1_out), .Q(rWout), .clk(clk), .clr(rst));
  Register #(.width(1)) register_4 (.D(lh), .en(not_1_out), .Q(lhout), .clk(clk), .clr(rst));
  Register #(.width(1)) register_5 (.D(RegWrite), .en(not_1_out), .Q(RegWriteout), .clk(clk), .clr(rst));
  Register #(.width(1)) register_6 (.D(Stopin), .en(not_1_out), .Q(Stopout), .clk(clk), .clr(rst));
endmodule
